// Logisim project CPU-integration_test.circ as structural Verilog: 1 circuit, main circuit main
module main (
  output [31:0] ra,
  output [31:0] sp,
  output [31:0] t0,
  output [31:0] t1,
  output [31:0] t2,
  output [31:0] s0,
  output [31:0] s1,
  output [31:0] a0,
  output [31:0] Requested_Address,
  output [31:0] Requested_Instruction,
  output [15:0] Time_Step,
  output halt
);

  wire clk;

  Clock clock_1 (.out(clk));
  // Probe on Requested_Address
  ROM #(.addrWidth(14), .dataWidth(32)) rom_1 (.addr(Requested_Address[15:2]), .data(Requested_Instruction));
  cpu_main main_1 (
    .INSTRUCTION(Requested_Instruction), .CLOCK(clk), .ra(ra), .sp(sp), .t0(t0), .t1(t1), .t2(t2), .s0(s0),
    .s1(s1), .a0(a0), .PROGRAM_COUNTER(Requested_Address));
  // Probe on Requested_Instruction
  Counter #(.width(16), .max('hffff)) counter_1 (.clk(clk), .Q(Time_Step));  // open: clr, load, up, count, D, carry
  Comparator #(.width(16)) comparator_1 (.a(Time_Step), .b(16'h1c), .eq(halt));  // open: gt, lt

  // Other names for the same wires on the sheet: fetch_addr[31:0] = Requested_Address;
  //   Instruction[31:0] = Requested_Instruction

  // Notes on the sheet:
  //   contents of rom_1 (hex, n*v repeats v):
  //   0010F437 FFF00493 7E812E23 7E912C23 018000E7 009422B3 00028663 00029E63 40940433 7FD10283 7FE11303
  //   7F812383 7E512823 00734263 029402B3 02941333 028433B3 7E512623 008000EF 007302B3 00545433 006494B3
  //   00944533 0002F293 FFF36313 0262E263 00229293 00235313 4043D393 00400493 029452B3 02947333 0002C293
  //   7E512C23 00007033
  //   YOUR CPU SHOULD FIT IN HERE!
  //   Instruction Memory
  //   Halts Execution After Constant # of Clock Cycles
  //   Constant
endmodule
