// Logisim project alu.circ as structural Verilog: 1 circuit, main circuit alu
module alu (
  input  [31:0] A,
  input  [31:0] B,
  input  [3:0] ALUSel,
  output [31:0] out_4,
  output [31:0] Result
);

  wire and_2_out, and_3_out, not_3_out, not_6_out, or_2_out;
  wire [31:0] add0, adder_2_out, adder_3_out, adder_4_out, adder_5_out, and1, divider_2_out, divu8, mul10,
       mulh14, mulhu11, multiplexer_2_out, multiplexer_4_out, multiplexer_5_out, multiplexer_6_out,
       multiplier_2_cout, multiplier_3_out, multiplier_4_cout, multiplier_4_out, not_1_out, not_2_out,
       not_4_out, not_5_out, or2, remu9, sll6, slt7, sra5, srl4, sub12, subtractor_1_out, xor3;

  Shifter #(.width(32), .shift("lr")) shifter_1 (.in(A), .\dist (B[4:0]), .out(srl4));
  Shifter #(.width(32), .shift("ar")) shifter_2 (.in(A), .\dist (B[4:0]), .out(sra5));
  Shifter #(.width(32)) shifter_3 (.in(A), .\dist (B[4:0]), .out(sll6));
  Multiplexer #(.select(4), .width(32), .enable("false")) multiplexer_1 (
    .in0(add0), .in1(and1), .in2(or2), .in3(xor3), .in4(srl4), .in5(sra5), .in6(sll6), .in7(slt7),
    .in8(divu8), .in9(remu9), .in10(mul10), .in11(mulhu11), .in12(sub12), .in13(B), .in14(mulh14),
    .out(Result), .sel(ALUSel));  // open: in15
  Adder #(.width(32)) adder_1 (.a(A), .b(B), .out(add0));  // open: cin, cout
  assign and1 = A & B;  // AND_Gate and_1, 32 bits wide
  assign or2 = A | B;  // OR_Gate or_1, 32 bits wide
  assign xor3 = A ^ B;  // XOR_Gate xor_1, 32 bits wide
  assign not_1_out = ~A;  // NOT_Gate not_1, 32 bits wide
  assign not_2_out = ~B;  // NOT_Gate not_2, 32 bits wide
  Subtractor #(.width(32)) subtractor_1 (.a(A), .b(B), .out(subtractor_1_out));  // open: bin, bout
  Divider #(.width(32)) divider_1 (.a(A), .b(B), .out(divu8));  // open: upper, rem
  Divider #(.width(32)) divider_2 (.a(A), .b(B), .out(divider_2_out));  // open: upper, rem
  Multiplier #(.width(32)) multiplier_1 (.a(A), .b(B), .out(mul10), .cout(mulhu11));  // open: cin
  Subtractor #(.width(32)) subtractor_2 (.a(A), .b(B), .out(sub12));  // open: bin, bout
  Multiplier #(.width(32)) multiplier_2 (.a(A), .b(B), .cout(multiplier_2_cout));  // open: out, cin
  Multiplexer #(.width(32), .enable("false")) multiplexer_2 (
    .in0(A), .in1(adder_2_out), .out(multiplexer_2_out), .sel(A[31]));
  Adder #(.width(32)) adder_2 (.a(not_1_out), .b(32'h1), .out(adder_2_out));  // open: cin, cout
  Adder #(.width(32)) adder_3 (.a(not_2_out), .b(32'h1), .out(adder_3_out));  // open: cin, cout
  Multiplexer #(.width(32), .enable("false")) multiplexer_3 (
    .in0({32{1'b0}}), .in1(32'h1), .out(slt7), .sel(subtractor_1_out[31]));
  Multiplier #(.width(32)) multiplier_3 (.a(divider_2_out), .b(B), .out(multiplier_3_out));  // open: cin, cout
  Multiplexer #(.width(32), .enable("false")) multiplexer_4 (
    .in0(B), .in1(adder_3_out), .out(multiplexer_4_out), .sel(B[31]));
  Subtractor #(.width(32)) subtractor_3 (.a(A), .b(multiplier_3_out), .out(remu9));  // open: bin, bout
  Multiplier #(.width(32)) multiplier_4 (
    .a(multiplexer_2_out), .b(multiplexer_4_out), .out(multiplier_4_out), .cout(multiplier_4_cout));  // open: cin
  or or_2 (or_2_out, A[31], B[31]);
  not not_3 (not_3_out, multiplier_4_out[31]);
  assign not_4_out = ~multiplier_4_out;  // NOT_Gate not_4, 32 bits wide
  assign not_5_out = ~multiplier_4_cout;  // NOT_Gate not_5, 32 bits wide
  Adder #(.width(32)) adder_4 (.a(not_5_out), .b(32'h1), .out(adder_4_out));  // open: cin, cout
  Adder #(.width(32)) adder_5 (.a(not_4_out), .b(32'h1), .out(adder_5_out));  // open: cin, cout
  not not_6 (not_6_out, adder_5_out[31]);
  Multiplexer #(.width(32), .enable("false")) multiplexer_5 (
    .in0(not_5_out), .in1(adder_4_out), .out(multiplexer_5_out), .sel(and_3_out));
  and and_2 (and_2_out, A[31], B[31]);
  and and_3 (and_3_out, not_3_out, not_6_out);
  Multiplexer #(.width(32), .enable("false")) multiplexer_6 (
    .in0(multiplexer_5_out), .in1(multiplier_4_cout), .out(multiplexer_6_out), .sel(and_2_out));
  Multiplexer #(.width(32), .enable("false")) multiplexer_7 (
    .in0(multiplier_2_cout), .in1(multiplexer_6_out), .out(mulh14), .sel(or_2_out));

  assign out_4 = A;

  // Other names for the same wires on the sheet: bsel13[31:0] = B

  // Notes on the sheet:
  //   INPUTS to your circuit
  //   DON'T CHANGE THE LOCATIONS OF THE INPUTS AND OUTPUTS!
  //   OUTPUT from your circuit
endmodule
