// Logisim project cpu.circ as structural Verilog: 3 circuits, main circuit main
module main (
  input  [31:0] INSTRUCTION,
  input  CLOCK,
  output [31:0] PROGRAM_COUNTER,
  output [31:0] ra,
  output [31:0] sp,
  output [31:0] t0,
  output [31:0] t1,
  output [31:0] t2,
  output [31:0] s0,
  output [31:0] s1,
  output [31:0] a0
);

  wire adder_3_cout, ALUSrc, and_1_out, and_2_out, and_3_out, and_4_out, and_5_out, and_6_out, and_7_out,
       and_8_out, and_9_out, and_10_out, and_11_out, and_12_out, and_13_out, and_14_out, and_15_out,
       and_16_out, branch, DMEM_p1, DMEM_p6, jump, lh_op, MemtoReg, MemWr, not_1_out, not_2_out, not_3_out,
       not_4_out, not_5_out, not_6_out, not_7_out, not_8_out, not_9_out, not_10_out, not_11_out, not_12_out,
       not_13_out, not_14_out, not_15_out, not_16_out, not_17_out, not_18_out, not_19_out, not_20_out,
       not_21_out, not_22_out, not_23_out, not_24_out, not_25_out, not_26_out, not_27_out, not_28_out,
       not_29_out, not_30_out, not_31_out, not_32_out, not_33_out, not_34_out, not_35_out, not_36_out,
       not_37_out, not_38_out, not_39_out, not_40_out, not_41_out, not_42_out, not_43_out, not_44_out,
       not_45_out, not_46_out, not_47_out, not_48_out, not_49_out, not_50_out, not_51_out, not_52_out,
       not_53_out, not_54_out, not_55_out, not_56_out, not_57_out, not_58_out, not_59_out, not_60_out,
       not_61_out, not_62_out, not_63_out, not_64_out, not_65_out, not_66_out, not_67_out, not_68_out,
       not_69_out, not_70_out, not_71_out, not_72_out, not_73_out, not_74_out, not_75_out, not_76_out,
       not_77_out, not_78_out, not_79_out, not_80_out, not_81_out, not_82_out, not_83_out, not_84_out,
       nPCsel, or_1_out, or_2_out, RegWr;
  wire [1:0] lb_op, LoadOp;
  wire [2:0] ExtOp, funct3, subtractor_4_out, subtractor_6_out, subtractor_8_out, subtractor_10_out;
  wire [3:0] ALUctr;
  wire [4:0] rd, rs1, rs2;
  wire [6:0] funct7, opcode, subtractor_1_out, subtractor_5_out, subtractor_7_out, subtractor_9_out,
       subtractor_11_out;
  wire [31:0] adder_1_out, adder_2_out, adder_3_out, adder_4_out, adder_5_out, Arithmetic_Logic_Unit_result,
       bit_extender_3_out, bit_extender_4_out, bit_extender_5_out, bit_extender_6_out, bit_extender_7_out,
       bit_extender_8_out, divider_1_out, divider_2_out, DMEM_p8, imme, immediategenerator_1_i,
       immediategenerator_1_s, immediategenerator_1_sb, immediategenerator_1_u, immediategenerator_1_uj,
       instruction_t, JPC, multiplexer_4_out, multiplexer_5_out, multiplexer_6_out, multiplexer_8_out,
       multiplexer_9_out, multiplexer_10_out, multiplexer_11_out, multiplier_1_out, multiplier_2_out, PC,
       PROGRAM_COUNTER_EX, Readdata1, Readdata2, register_4_q, subtractor_2_out, subtractor_3_out;

  Register #(.width(32)) register_1 (.D(PC), .en(1'b1), .clk(CLOCK), .Q(PROGRAM_COUNTER));  // open: clr
  Register #(.width(32)) register_2 (.D(PROGRAM_COUNTER), .clk(CLOCK), .Q(PROGRAM_COUNTER_EX));  // open: en, clr
  Register #(.width(32)) register_3 (
    .D(instruction_t), .en(1'b1), .clk(CLOCK), .Q({funct7, rs2, rs1, funct3, rd, opcode}));  // open: clr
  Register #(.width(32)) register_4 (.D(instruction_t), .en(1'b1), .clk(CLOCK), .Q(register_4_q));  // open: clr
  Multiplexer #(.width(32), .enable("false")) multiplexer_1 (
    .in0(INSTRUCTION), .in1(32'h13), .out(instruction_t), .sel(or_1_out));
  or or_1 (or_1_out, branch, jump);
  immediateGenerator immediategenerator_1 (
    .INSTRUCTION({funct7, rs2, rs1, funct3, rd, opcode}), .I(immediategenerator_1_i),
    .S(immediategenerator_1_s), .SB(immediategenerator_1_sb), .U(immediategenerator_1_u),
    .UJ(immediategenerator_1_uj));
  control control_1 (
    .INSTRUCTION(register_4_q), .MemWr(MemWr), .nPCsel(nPCsel), .RegWr(RegWr), .ExtOp(ExtOp),
    .ALUsrc(ALUSrc), .ALUctr(ALUctr), .MemtoReg(MemtoReg), .jump(jump), .LoadOp(LoadOp));
  Multiplexer #(.select(3), .width(32), .enable("false")) multiplexer_2 (
    .in0(immediategenerator_1_i), .in1(immediategenerator_1_s), .in2(immediategenerator_1_sb),
    .in3(immediategenerator_1_u), .in4(immediategenerator_1_uj), .out(imme), .sel(ExtOp));  // open: in5, in6, in7
  regfile_main RegFile (
    .rs2(rs2), .rd(rd), .Read_Data_1(Readdata1), .Read_Data_2(Readdata2), .ra(ra), .sp(sp), .t0(t0), .t1(t1),
    .t2(t2), .s0(s0), .s1(s1), .a0(a0), .rs1(rs1), .Write_Data(multiplexer_4_out), .RegWEn(RegWr), .clk(CLOCK));
  not not_1 (not_1_out, funct3[0]);
  not not_2 (not_2_out, funct3[1]);
  not not_3 (not_3_out, funct3[2]);
  Subtractor #(.width(7)) subtractor_1 (.a(opcode), .b(7'b1100111), .out(subtractor_1_out));  // open: bin, bout
  Adder #(.width(32)) adder_1 (.a(PROGRAM_COUNTER_EX), .b(imme), .out(adder_1_out));  // open: cin, cout
  Multiplexer #(.width(32), .enable("false")) multiplexer_3 (
    .in0(adder_1_out), .in1(adder_2_out), .out(JPC), .sel(and_3_out));
  Adder #(.width(32)) adder_2 (.a(imme), .b(Readdata1), .out(adder_2_out));  // open: cin, cout
  and and_1 (and_1_out, not_1_out, not_2_out, not_3_out);
  not not_4 (not_4_out, subtractor_1_out[0]);
  not not_5 (not_5_out, subtractor_1_out[1]);
  not not_6 (not_6_out, subtractor_1_out[2]);
  and and_2 (and_2_out, not_4_out, not_5_out, not_6_out, not_7_out, not_8_out, not_9_out, not_10_out);
  not not_7 (not_7_out, subtractor_1_out[3]);
  not not_8 (not_8_out, subtractor_1_out[4]);
  not not_9 (not_9_out, subtractor_1_out[5]);
  not not_10 (not_10_out, subtractor_1_out[6]);
  Multiplexer #(.width(32), .enable("false")) multiplexer_4 (
    .in0(multiplexer_8_out), .in1(adder_5_out), .out(multiplexer_4_out), .sel(jump));
  and and_3 (and_3_out, and_1_out, and_2_out);
  Adder #(.width(32)) adder_3 (.a(PROGRAM_COUNTER), .b(32'h4), .out(adder_3_out), .cout(adder_3_cout));  // open: cin
  Adder #(.width(32)) adder_4 (.a(PROGRAM_COUNTER_EX), .b(imme), .out(adder_4_out));  // open: cin, cout
  Multiplexer #(.width(32), .enable("false")) multiplexer_5 (
    .in0(Readdata2), .in1(imme), .out(multiplexer_5_out), .sel(ALUSrc));
  Multiplexer #(.width(32), .enable("false")) multiplexer_6 (
    .in0(adder_3_out), .in1(adder_4_out), .out(multiplexer_6_out), .sel(branch));
  alu Arithmetic_Logic_Unit (
    .ALUSel(ALUctr), .B(multiplexer_5_out), .A(Readdata1), .Result(Arithmetic_Logic_Unit_result));  // open: out_4
  Adder #(.width(32)) adder_5 (.a(PROGRAM_COUNTER_EX), .b(32'h4), .out(adder_5_out));  // open: cin, cout
  Multiplexer #(.width(32), .enable("false")) multiplexer_7 (.in0(multiplexer_6_out), .in1(JPC), .out(PC), .sel(jump));
  Multiplexer #(.select(2), .width(32), .enable("false")) multiplexer_8 (
    .in0(multiplexer_9_out), .in1(multiplexer_10_out), .in2(multiplexer_11_out), .out(multiplexer_8_out),
    .sel(LoadOp));  // open: in3
  Divider #(.width(32)) divider_1 (.a(imme), .b(32'h2), .out(divider_1_out));  // open: upper, rem
  Divider #(.width(32)) divider_2 (.a(imme), .b(32'h4), .out(divider_2_out));  // open: upper, rem
  Multiplier #(.width(32)) multiplier_1 (.a(divider_1_out), .b(32'h2), .out(multiplier_1_out));  // open: cin, cout
  Multiplier #(.width(32)) multiplier_2 (.a(divider_2_out), .b(32'h4), .out(multiplier_2_out));  // open: cin, cout
  // mem_main DMEM: pin names not known; wires that end beside it: DMEM_p1, Arithmetic_Logic_Unit_result, Readdata2, DMEM_p1, CLOCK, DMEM_p6, MemWr, DMEM_p8
  Subtractor #(.width(32)) subtractor_2 (.a(imme), .b(multiplier_1_out), .out(subtractor_2_out));  // open: bin, bout
  Bit_Extender #(.in_width(32), .out_width(1)) bit_extender_1 (.in(subtractor_2_out), .out(lh_op));
  Subtractor #(.width(32)) subtractor_3 (.a(imme), .b(multiplier_2_out), .out(subtractor_3_out));  // open: bin, bout
  Bit_Extender #(.in_width(32), .out_width(2)) bit_extender_2 (.in(subtractor_3_out), .out(lb_op));
  Multiplexer #(.width(32), .enable("false")) multiplexer_9 (
    .in0(Arithmetic_Logic_Unit_result), .in1(DMEM_p8), .out(multiplexer_9_out), .sel(MemtoReg));
  not not_11 (not_11_out, Arithmetic_Logic_Unit_result[0]);
  not not_12 (not_12_out, Arithmetic_Logic_Unit_result[1]);
  not not_13 (not_13_out, Arithmetic_Logic_Unit_result[2]);
  not not_14 (not_14_out, Arithmetic_Logic_Unit_result[3]);
  not not_15 (not_15_out, Arithmetic_Logic_Unit_result[4]);
  not not_16 (not_16_out, Arithmetic_Logic_Unit_result[5]);
  not not_17 (not_17_out, Arithmetic_Logic_Unit_result[6]);
  not not_18 (not_18_out, Arithmetic_Logic_Unit_result[7]);
  not not_19 (not_19_out, Arithmetic_Logic_Unit_result[8]);
  not not_20 (not_20_out, Arithmetic_Logic_Unit_result[9]);
  not not_21 (not_21_out, Arithmetic_Logic_Unit_result[10]);
  not not_22 (not_22_out, Arithmetic_Logic_Unit_result[11]);
  not not_23 (not_23_out, Arithmetic_Logic_Unit_result[12]);
  not not_24 (not_24_out, Arithmetic_Logic_Unit_result[13]);
  not not_25 (not_25_out, Arithmetic_Logic_Unit_result[14]);
  not not_26 (not_26_out, Arithmetic_Logic_Unit_result[15]);
  not not_27 (not_27_out, Arithmetic_Logic_Unit_result[16]);
  not not_28 (not_28_out, Arithmetic_Logic_Unit_result[17]);
  not not_29 (not_29_out, Arithmetic_Logic_Unit_result[18]);
  not not_30 (not_30_out, Arithmetic_Logic_Unit_result[19]);
  not not_31 (not_31_out, Arithmetic_Logic_Unit_result[20]);
  not not_32 (not_32_out, Arithmetic_Logic_Unit_result[21]);
  not not_33 (not_33_out, Arithmetic_Logic_Unit_result[22]);
  not not_34 (not_34_out, Arithmetic_Logic_Unit_result[23]);
  not not_35 (not_35_out, Arithmetic_Logic_Unit_result[24]);
  not not_36 (not_36_out, Arithmetic_Logic_Unit_result[25]);
  not not_37 (not_37_out, Arithmetic_Logic_Unit_result[26]);
  not not_38 (not_38_out, Arithmetic_Logic_Unit_result[27]);
  not not_39 (not_39_out, Arithmetic_Logic_Unit_result[28]);
  not not_40 (not_40_out, Arithmetic_Logic_Unit_result[29]);
  not not_41 (not_41_out, Arithmetic_Logic_Unit_result[30]);
  not not_42 (not_42_out, Arithmetic_Logic_Unit_result[31]);
  and and_4 (and_4_out, not_11_out, not_12_out, not_13_out, not_14_out, not_15_out, not_16_out, not_17_out, not_18_out, not_19_out, not_20_out, not_21_out, not_22_out, not_23_out, not_24_out, not_25_out, not_26_out, not_27_out, not_28_out, not_29_out, not_30_out, not_31_out, not_32_out, not_33_out, not_34_out, not_35_out, not_36_out, not_37_out, not_38_out, not_39_out, not_40_out, not_41_out, not_42_out);
  assign bit_extender_3_out = {{16{multiplexer_9_out[31]}}, multiplexer_9_out[31:16]};  // Bit_Extender bit_extender_3
  assign bit_extender_4_out = {{16{multiplexer_9_out[15]}}, multiplexer_9_out[15:0]};  // Bit_Extender bit_extender_4
  assign bit_extender_5_out = {{24{multiplexer_9_out[31]}}, multiplexer_9_out[31:24]};  // Bit_Extender bit_extender_5
  assign bit_extender_6_out = {{24{multiplexer_9_out[23]}}, multiplexer_9_out[23:16]};  // Bit_Extender bit_extender_6
  assign bit_extender_7_out = {{24{multiplexer_9_out[15]}}, multiplexer_9_out[15:8]};  // Bit_Extender bit_extender_7
  assign bit_extender_8_out = {{24{multiplexer_9_out[7]}}, multiplexer_9_out[7:0]};  // Bit_Extender bit_extender_8
  Multiplexer #(.width(32), .enable("false")) multiplexer_10 (
    .in0(bit_extender_3_out), .in1(bit_extender_4_out), .out(multiplexer_10_out), .sel(lh_op));
  Multiplexer #(.select(2), .width(32), .enable("false")) multiplexer_11 (
    .in0(bit_extender_5_out), .in1(bit_extender_6_out), .in2(bit_extender_7_out), .in3(bit_extender_8_out),
    .out(multiplexer_11_out), .sel(lb_op));
  Subtractor #(.width(3)) subtractor_4 (.a(funct3), .b(3'b000), .out(subtractor_4_out));  // open: bin, bout
  Subtractor #(.width(7)) subtractor_5 (.a(opcode), .b(7'b1100011), .out(subtractor_5_out));  // open: bin, bout
  Subtractor #(.width(3)) subtractor_6 (.a(funct3), .b(3'b100), .out(subtractor_6_out));  // open: bin, bout
  Subtractor #(.width(7)) subtractor_7 (.a(opcode), .b(7'b1100011), .out(subtractor_7_out));  // open: bin, bout
  Subtractor #(.width(3)) subtractor_8 (.a(funct3), .b(3'b110), .out(subtractor_8_out));  // open: bin, bout
  Subtractor #(.width(7)) subtractor_9 (.a(opcode), .b(7'b1100011), .out(subtractor_9_out));  // open: bin, bout
  Subtractor #(.width(3)) subtractor_10 (.a(funct3), .b(3'b001), .out(subtractor_10_out));  // open: bin, bout
  Subtractor #(.width(7)) subtractor_11 (.a(opcode), .b(7'b1100011), .out(subtractor_11_out));  // open: bin, bout
  not not_43 (not_43_out, subtractor_4_out[0]);
  not not_44 (not_44_out, subtractor_4_out[1]);
  not not_45 (not_45_out, subtractor_4_out[2]);
  not not_46 (not_46_out, subtractor_5_out[0]);
  not not_47 (not_47_out, subtractor_5_out[1]);
  not not_48 (not_48_out, subtractor_5_out[2]);
  not not_49 (not_49_out, subtractor_5_out[3]);
  not not_50 (not_50_out, subtractor_5_out[4]);
  not not_51 (not_51_out, subtractor_5_out[5]);
  not not_52 (not_52_out, subtractor_5_out[6]);
  not not_53 (not_53_out, subtractor_6_out[0]);
  not not_54 (not_54_out, subtractor_6_out[1]);
  not not_55 (not_55_out, subtractor_6_out[2]);
  not not_56 (not_56_out, subtractor_7_out[0]);
  not not_57 (not_57_out, subtractor_7_out[1]);
  not not_58 (not_58_out, subtractor_7_out[2]);
  not not_59 (not_59_out, subtractor_7_out[3]);
  not not_60 (not_60_out, subtractor_7_out[4]);
  not not_61 (not_61_out, subtractor_7_out[5]);
  not not_62 (not_62_out, subtractor_7_out[6]);
  not not_63 (not_63_out, and_4_out);
  not not_64 (not_64_out, subtractor_8_out[0]);
  not not_65 (not_65_out, subtractor_8_out[1]);
  not not_66 (not_66_out, subtractor_8_out[2]);
  not not_67 (not_67_out, subtractor_9_out[0]);
  not not_68 (not_68_out, subtractor_9_out[1]);
  not not_69 (not_69_out, subtractor_9_out[2]);
  not not_70 (not_70_out, subtractor_9_out[3]);
  not not_71 (not_71_out, subtractor_9_out[4]);
  not not_72 (not_72_out, subtractor_9_out[5]);
  not not_73 (not_73_out, subtractor_9_out[6]);
  not not_74 (not_74_out, subtractor_10_out[0]);
  not not_75 (not_75_out, subtractor_10_out[1]);
  not not_76 (not_76_out, subtractor_10_out[2]);
  not not_77 (not_77_out, subtractor_11_out[0]);
  not not_78 (not_78_out, subtractor_11_out[1]);
  not not_79 (not_79_out, subtractor_11_out[2]);
  not not_80 (not_80_out, subtractor_11_out[3]);
  not not_81 (not_81_out, subtractor_11_out[4]);
  not not_82 (not_82_out, subtractor_11_out[5]);
  not not_83 (not_83_out, subtractor_11_out[6]);
  not not_84 (not_84_out, and_4_out);
  and and_5 (and_5_out, not_43_out, not_44_out, not_45_out);
  and and_6 (and_6_out, not_46_out, not_47_out, not_48_out, not_49_out, not_50_out, not_51_out, not_52_out);
  and and_7 (and_7_out, not_53_out, not_54_out, not_55_out);
  and and_8 (and_8_out, not_56_out, not_57_out, not_58_out, not_59_out, not_60_out, not_61_out, not_62_out);
  and and_9 (and_9_out, not_64_out, not_65_out, not_66_out);
  and and_10 (and_10_out, not_67_out, not_68_out, not_69_out, not_70_out, not_71_out, not_72_out, not_73_out);
  and and_11 (and_11_out, not_74_out, not_75_out, not_76_out);
  and and_12 (and_12_out, not_77_out, not_78_out, not_79_out, not_80_out, not_81_out, not_82_out, not_83_out);
  and and_13 (and_13_out, and_5_out, and_6_out, and_4_out);
  and and_14 (and_14_out, and_7_out, and_8_out, not_63_out);
  and and_15 (and_15_out, and_9_out, and_10_out, and_4_out);
  and and_16 (and_16_out, and_11_out, and_12_out, not_84_out);
  Multiplexer #(.enable("false")) multiplexer_12 (.in0(1'b0), .in1(or_2_out), .out(branch), .sel(nPCsel));
  or or_2 (or_2_out, and_13_out, and_14_out, and_15_out, and_16_out);

  // Other names for the same wires on the sheet: clk = CLOCK

  // Notes on the sheet:
  //   Output
  //   IMEM (do **NOT** move this)
  //   Inputs
  //   Inputs/Outputs for testing. Do **NOT** move these.
endmodule

module immediateGenerator (
  input  [31:0] INSTRUCTION,
  output [31:0] I,
  output [31:0] S,
  output [31:0] SB,
  output [31:0] U,
  output [31:0] UJ
);

  assign I = {{20{INSTRUCTION[31]}}, INSTRUCTION[31:20]};  // Bit_Extender bit_extender_1
  assign S = {{20{INSTRUCTION[31]}}, {INSTRUCTION[31:25], INSTRUCTION[11:7]}};  // Bit_Extender bit_extender_2
  assign SB = {{19{INSTRUCTION[31]}}, {INSTRUCTION[31], INSTRUCTION[7], INSTRUCTION[30:25], INSTRUCTION[11:8], 1'b0}};  // Bit_Extender bit_extender_3
  assign UJ = {{11{INSTRUCTION[31]}}, {INSTRUCTION[31], INSTRUCTION[19:12], INSTRUCTION[20], INSTRUCTION[30:21], 1'b0}};  // Bit_Extender bit_extender_4

  assign U = {INSTRUCTION[31:12], {12{1'b0}}};
endmodule
module control (
  input  [31:0] INSTRUCTION,
  output MemWr,
  output nPCsel,
  output RegWr,
  output [2:0] ExtOp,
  output ALUsrc,
  output [3:0] ALUctr,
  output MemtoReg,
  output jump,
  output [1:0] LoadOp
);

  wire and_1_out, and_2_out, and_3_out, and_4_out, and_5_out, and_6_out, and_7_out, and_8_out, and_9_out,
       and_10_out, and_11_out, and_12_out, and_13_out, and_14_out, and_15_out, and_16_out, and_17_out,
       and_18_out, and_19_out, and_22_out, and_23_out, and_24_out, and_27_out, and_30_out, and_31_out,
       and_32_out, and_33_out, and_34_out, and_35_out, and_36_out, and_37_out, and_38_out, and_39_out,
       and_40_out, and_41_out, and_42_out, and_43_out, and_44_out, and_45_out, and_46_out, and_47_out,
       and_48_out, and_49_out, and_50_out, and_51_out, and_52_out, and_53_out, and_54_out, and_55_out,
       and_56_out, and_57_out, and_58_out, and_59_out, and_60_out, and_61_out, and_62_out, and_63_out,
       and_64_out, and_65_out, and_66_out, and_67_out, and_68_out, and_69_out, and_70_out, and_71_out,
       and_72_out, and_73_out, and_74_out, and_75_out, and_76_out, and_77_out, and_78_out, and_79_out,
       and_80_out, and_81_out, and_82_out, and_83_out, and_84_out, and_85_out, and_86_out, and_87_out,
       and_88_out, and_89_out, and_90_out, and_91_out, and_92_out, and_93_out, and_94_out, and_95_out,
       and_96_out, and_97_out, and_98_out, and_99_out, and_100_out, and_101_out, and_102_out, and_103_out,
       and_104_out, and_105_out, and_106_out, and_107_out, and_108_out, and_109_out, and_110_out,
       and_111_out, and_112_out, and_113_out, and_114_out, and_115_out, and_116_out, and_117_out,
       and_118_out, and_119_out, and_120_out, and_121_out, and_122_out, and_123_out, and_124_out,
       and_125_out, and_126_out, and_127_out, and_128_out, and_129_out, and_130_out, and_131_out,
       and_132_out, and_133_out, and_134_out, and_135_out, and_136_out, and_137_out, and_138_out,
       and_139_out, and_140_out, and_141_out, and_142_out, and_143_out, and_144_out, and_145_out,
       and_146_out, and_147_out, and_148_out, and_149_out, and_150_out, and_151_out, and_152_out,
       and_153_out, and_154_out, and_155_out, and_156_out, and_157_out, and_158_out, and_159_out,
       and_160_out, and_161_out, and_162_out, and_163_out, and_164_out, and_165_out, and_166_out,
       and_167_out, and_168_out, and_169_out, and_170_out, and_171_out, and_172_out, and_173_out,
       and_174_out, and_175_out, and_176_out, and_177_out, and_178_out, and_179_out, and_180_out,
       and_181_out, and_182_out, and_183_out, and_184_out, and_185_out, and_186_out, and_187_out,
       and_188_out, and_189_out, not_1_out, not_2_out, not_3_out, not_4_out, not_5_out, not_6_out, not_7_out,
       not_8_out, not_9_out, not_10_out, not_11_out, not_12_out, not_13_out, not_14_out, not_15_out,
       not_16_out, not_17_out, not_18_out, not_19_out, not_20_out, not_21_out, not_22_out, not_23_out,
       not_24_out, not_25_out, not_26_out, not_27_out, not_28_out, not_29_out, not_30_out, not_31_out,
       not_32_out, not_33_out, not_34_out, not_35_out, not_36_out, not_37_out, not_38_out, not_39_out,
       not_40_out, not_41_out, not_42_out, not_43_out, not_44_out, not_45_out, not_46_out, not_47_out,
       not_48_out, not_49_out, not_50_out, not_51_out, not_52_out, not_53_out, not_54_out, not_55_out,
       not_56_out, not_57_out, not_58_out, not_59_out, not_60_out, not_61_out, not_62_out, not_63_out,
       not_64_out, not_65_out, not_66_out, not_67_out, not_68_out, not_69_out, not_70_out, not_71_out,
       not_72_out, not_73_out, not_74_out, not_75_out, not_76_out, not_77_out, not_78_out, not_79_out,
       not_80_out, not_81_out, not_82_out, not_83_out, not_84_out, not_85_out, not_86_out, not_87_out,
       not_88_out, not_89_out, not_90_out, not_91_out, not_92_out, not_93_out, not_94_out, not_95_out,
       not_96_out, not_97_out, not_98_out, not_99_out, not_100_out, not_101_out, not_102_out, not_103_out,
       not_104_out, not_105_out, not_106_out, not_107_out, not_108_out, not_109_out, not_110_out,
       not_111_out, not_112_out, not_113_out, not_114_out, not_115_out, not_116_out, not_117_out,
       not_118_out, not_119_out, not_120_out, not_121_out, not_122_out, not_123_out, not_124_out,
       not_125_out, not_126_out, not_127_out, not_128_out, not_129_out, not_130_out, not_131_out,
       not_132_out, not_133_out, not_134_out, not_135_out, not_136_out, not_137_out, not_138_out,
       not_139_out, not_140_out, not_141_out, not_142_out, not_143_out, not_144_out, not_145_out,
       not_146_out, not_147_out, not_148_out, not_149_out, not_150_out, not_151_out, not_152_out,
       not_153_out, not_154_out, not_155_out, not_156_out, not_157_out, not_158_out, not_159_out,
       not_160_out, not_161_out, not_162_out, not_163_out, not_164_out, not_165_out, not_166_out,
       not_167_out, not_168_out, not_169_out, not_170_out, not_171_out, not_172_out, not_173_out,
       not_174_out, not_175_out, not_176_out, not_177_out, not_178_out, not_179_out, not_180_out,
       not_181_out, not_182_out, not_183_out, not_184_out, not_185_out, not_186_out, not_187_out,
       not_188_out, not_189_out, not_190_out, not_191_out, not_192_out, not_193_out, not_194_out,
       not_195_out, not_196_out, not_197_out, not_198_out, not_199_out, not_200_out, not_201_out,
       not_202_out, not_203_out, not_204_out, not_205_out, not_206_out, not_207_out, not_208_out,
       not_209_out, not_210_out, not_211_out, not_212_out, not_213_out, not_214_out, not_215_out,
       not_216_out, not_217_out, not_218_out, not_219_out, not_220_out, not_221_out, not_222_out,
       not_223_out, not_224_out, not_225_out, not_226_out, not_227_out, not_228_out, not_229_out,
       not_230_out, not_231_out, not_232_out, not_233_out, not_234_out, not_235_out, not_236_out,
       not_237_out, not_238_out, not_239_out, not_240_out, not_241_out, not_242_out, not_243_out,
       not_244_out, not_245_out, not_246_out, not_247_out, not_248_out, not_249_out, not_250_out,
       not_251_out, not_252_out, not_253_out, not_254_out, not_255_out, not_256_out, not_257_out,
       not_258_out, not_259_out, not_260_out, not_261_out, not_262_out, not_263_out, not_264_out,
       not_265_out, not_266_out, not_267_out, not_268_out, not_269_out, not_270_out, not_271_out,
       not_272_out, not_273_out, not_274_out, not_275_out, not_276_out, not_277_out, not_278_out,
       not_279_out, not_280_out, not_281_out, not_282_out, not_283_out, not_284_out, not_285_out,
       not_286_out, not_287_out, not_288_out, not_289_out, not_290_out, not_291_out, not_292_out,
       not_293_out, not_294_out, not_295_out, not_296_out, not_297_out, not_298_out, not_299_out,
       not_300_out, not_301_out, not_302_out, not_303_out, not_304_out, not_305_out, not_306_out,
       not_307_out, not_308_out, not_309_out, not_310_out, not_311_out, not_312_out, not_313_out,
       not_314_out, not_315_out, not_316_out, not_317_out, not_318_out, not_319_out, not_320_out,
       not_321_out, not_322_out, not_323_out, not_324_out, not_325_out, not_326_out, not_327_out,
       not_328_out, not_329_out, not_330_out, not_331_out, not_332_out, not_333_out, not_334_out,
       not_335_out, not_336_out, not_337_out, not_338_out, not_339_out, not_340_out, not_341_out,
       not_342_out, not_343_out, not_344_out, not_345_out, not_346_out, not_347_out, not_348_out,
       not_349_out, not_350_out, not_351_out, not_352_out, not_353_out, not_354_out, not_355_out,
       not_356_out, not_357_out, not_358_out, not_359_out, not_360_out, not_361_out, not_362_out,
       not_363_out, not_364_out, not_365_out, not_366_out, not_367_out, not_368_out, not_369_out,
       not_370_out, not_371_out, not_372_out, not_373_out, not_374_out, not_375_out, not_376_out,
       not_377_out, not_378_out, not_379_out, not_380_out, not_381_out, not_382_out, not_383_out,
       not_384_out, not_385_out, not_386_out, not_387_out, not_388_out, not_389_out, not_390_out,
       not_391_out, not_392_out, not_393_out, not_394_out, not_395_out, not_396_out, not_397_out,
       not_398_out, not_399_out, not_400_out, not_401_out, not_402_out, not_403_out, not_404_out,
       not_405_out, not_406_out, not_407_out, not_408_out, not_409_out, not_410_out, not_411_out,
       not_412_out, not_413_out, not_414_out, not_415_out, not_416_out, not_417_out, not_418_out,
       not_419_out, not_420_out, not_421_out, not_422_out, not_423_out, not_424_out, not_425_out,
       not_426_out, not_427_out, not_428_out, not_429_out, not_430_out, not_431_out, not_432_out,
       not_433_out, not_434_out, not_435_out, not_436_out, not_437_out, not_438_out, not_439_out,
       not_440_out, not_441_out, not_442_out, not_443_out, not_444_out, not_445_out, not_446_out,
       not_447_out, not_448_out, not_449_out, not_450_out, not_451_out, not_452_out, not_453_out,
       not_454_out, not_455_out, not_456_out, not_457_out, not_458_out, not_459_out, not_460_out,
       not_461_out, not_462_out, not_463_out, not_464_out, not_465_out, not_466_out, not_467_out,
       not_468_out, not_469_out, not_470_out, not_471_out, not_472_out, not_473_out, not_474_out,
       not_475_out, not_476_out, not_477_out, not_478_out, not_479_out, not_480_out, not_481_out,
       not_482_out, not_483_out, not_484_out, not_485_out, not_486_out, not_487_out, not_488_out,
       not_489_out, not_490_out, not_491_out, not_492_out, not_493_out, not_494_out, not_495_out,
       not_496_out, not_497_out, not_498_out, not_499_out, not_500_out, not_501_out, not_502_out,
       not_503_out, not_504_out, not_505_out, not_506_out, not_507_out, not_508_out, not_509_out,
       not_510_out, not_511_out, not_512_out, not_513_out, not_514_out, not_515_out, not_516_out,
       not_517_out, not_518_out, not_519_out, not_520_out, not_521_out, not_522_out, not_523_out,
       not_524_out, not_525_out, not_526_out, not_527_out, not_528_out, not_529_out, not_530_out,
       not_531_out, not_532_out, not_533_out, not_534_out, not_535_out, not_536_out, not_537_out,
       not_538_out, not_539_out, not_540_out, not_541_out, not_542_out, not_543_out, not_544_out,
       not_545_out, not_546_out, not_547_out, not_548_out, not_549_out, not_550_out, not_551_out,
       not_552_out, not_553_out, not_554_out, not_555_out, not_556_out, not_557_out, not_558_out,
       not_559_out, not_560_out, not_561_out, not_562_out, not_563_out, not_564_out, not_565_out,
       not_566_out, not_567_out, not_568_out, not_569_out, not_570_out, not_571_out, not_572_out,
       not_573_out, not_574_out, not_575_out, not_576_out, not_577_out, not_578_out, not_579_out,
       not_580_out, not_581_out, not_582_out, not_583_out, not_584_out, not_585_out, not_586_out,
       not_587_out, not_588_out, not_589_out, not_590_out, not_591_out, not_592_out, not_593_out,
       not_594_out, not_595_out, not_596_out, not_597_out, not_598_out, not_599_out, not_600_out,
       not_601_out, not_602_out, not_603_out, not_604_out, not_605_out, not_606_out, not_607_out,
       not_608_out, not_609_out, not_610_out, not_611_out, not_612_out, not_613_out, not_614_out,
       not_615_out, not_616_out, not_617_out, not_618_out, not_619_out, not_620_out, not_621_out,
       not_622_out, not_623_out, not_624_out, not_625_out, not_626_out, not_627_out, not_628_out,
       not_629_out, not_630_out, not_631_out, not_632_out, not_633_out, not_634_out, not_635_out,
       not_636_out, not_637_out, not_638_out, not_639_out, not_640_out, not_641_out, not_642_out,
       not_643_out, not_644_out, not_645_out, not_646_out, not_647_out, not_648_out, not_649_out,
       not_650_out, not_651_out, not_652_out, not_653_out, not_654_out, not_655_out, not_656_out,
       not_657_out, not_658_out, not_659_out, not_660_out, not_661_out, not_662_out, not_663_out,
       not_664_out, not_665_out, not_666_out, not_667_out, not_668_out, not_669_out, not_670_out,
       not_671_out, not_672_out, not_673_out, not_674_out, not_675_out, not_676_out, not_677_out,
       not_678_out, not_679_out, not_680_out, not_681_out, not_682_out, not_683_out, not_684_out,
       not_685_out, not_686_out, not_687_out, not_688_out, not_689_out, not_690_out, not_691_out,
       not_692_out, not_693_out, not_694_out, not_695_out, not_696_out, not_697_out, not_698_out,
       not_699_out, not_700_out, not_701_out, not_702_out, not_703_out, not_704_out, not_705_out,
       not_706_out, not_707_out, not_708_out, not_709_out, not_710_out, not_711_out, not_712_out,
       not_713_out, not_714_out, not_715_out, not_716_out, not_717_out, not_718_out, not_719_out,
       not_720_out, not_721_out, not_722_out, not_723_out, not_724_out, not_725_out, not_726_out,
       not_727_out, not_728_out, not_729_out, not_730_out, not_731_out, not_732_out, not_733_out,
       not_734_out, not_735_out, not_736_out, not_737_out, not_738_out, not_739_out, not_740_out,
       not_741_out, not_742_out, not_743_out, not_744_out, not_745_out, not_746_out, not_747_out,
       not_748_out, not_749_out, not_750_out, not_751_out, not_752_out, not_753_out, not_754_out,
       not_755_out, not_756_out, not_757_out, not_758_out, not_759_out, not_760_out, not_761_out,
       not_762_out, not_763_out, not_764_out, not_765_out, not_766_out, not_767_out, not_768_out,
       not_769_out, not_770_out, not_771_out, not_772_out, not_773_out, not_774_out, not_775_out,
       not_776_out, not_777_out, not_778_out, not_779_out, not_780_out, not_781_out, not_782_out,
       not_783_out, not_784_out, not_785_out, not_786_out, not_787_out, not_788_out, not_789_out,
       not_790_out, not_791_out, not_792_out, not_793_out, not_794_out, not_795_out, not_796_out,
       not_797_out, not_798_out, not_799_out, not_800_out, not_801_out, not_802_out, not_803_out,
       not_804_out, not_805_out, not_806_out, not_807_out, not_808_out, not_809_out, not_810_out,
       not_811_out, not_812_out, not_813_out, not_814_out, not_815_out, not_816_out, not_817_out;
  wire [2:0] subtractor_20_out, subtractor_21_out, subtractor_23_out, subtractor_27_out, subtractor_30_out,
       subtractor_33_out, subtractor_36_out, subtractor_39_out, subtractor_42_out, subtractor_44_out,
       subtractor_46_out, subtractor_49_out, subtractor_51_out, subtractor_68_out, subtractor_71_out,
       subtractor_73_out, subtractor_75_out, subtractor_77_out, subtractor_79_out, subtractor_80_out,
       subtractor_81_out, subtractor_82_out, subtractor_83_out, subtractor_84_out, subtractor_85_out,
       subtractor_86_out, subtractor_89_out, subtractor_92_out, subtractor_95_out, subtractor_98_out,
       subtractor_101_out, subtractor_104_out, subtractor_106_out, subtractor_109_out, subtractor_112_out,
       subtractor_114_out, subtractor_116_out, subtractor_119_out, subtractor_122_out, subtractor_125_out,
       subtractor_128_out, subtractor_131_out, subtractor_134_out, subtractor_137_out, subtractor_139_out,
       subtractor_142_out;
  wire [6:0] subtractor_1_out, subtractor_2_out, subtractor_3_out, subtractor_4_out, subtractor_5_out,
       subtractor_6_out, subtractor_7_out, subtractor_8_out, subtractor_9_out, subtractor_10_out,
       subtractor_11_out, subtractor_12_out, subtractor_13_out, subtractor_14_out, subtractor_15_out,
       subtractor_16_out, subtractor_17_out, subtractor_18_out, subtractor_19_out, subtractor_22_out,
       subtractor_24_out, subtractor_25_out, subtractor_26_out, subtractor_28_out, subtractor_29_out,
       subtractor_31_out, subtractor_32_out, subtractor_34_out, subtractor_35_out, subtractor_37_out,
       subtractor_38_out, subtractor_40_out, subtractor_41_out, subtractor_43_out, subtractor_45_out,
       subtractor_47_out, subtractor_48_out, subtractor_50_out, subtractor_52_out, subtractor_53_out,
       subtractor_54_out, subtractor_55_out, subtractor_56_out, subtractor_57_out, subtractor_58_out,
       subtractor_59_out, subtractor_60_out, subtractor_61_out, subtractor_62_out, subtractor_63_out,
       subtractor_64_out, subtractor_65_out, subtractor_66_out, subtractor_67_out, subtractor_69_out,
       subtractor_70_out, subtractor_72_out, subtractor_74_out, subtractor_76_out, subtractor_78_out,
       subtractor_87_out, subtractor_88_out, subtractor_90_out, subtractor_91_out, subtractor_93_out,
       subtractor_94_out, subtractor_96_out, subtractor_97_out, subtractor_99_out, subtractor_100_out,
       subtractor_102_out, subtractor_103_out, subtractor_105_out, subtractor_107_out, subtractor_108_out,
       subtractor_110_out, subtractor_111_out, subtractor_113_out, subtractor_115_out, subtractor_117_out,
       subtractor_118_out, subtractor_120_out, subtractor_121_out, subtractor_123_out, subtractor_124_out,
       subtractor_126_out, subtractor_127_out, subtractor_129_out, subtractor_130_out, subtractor_132_out,
       subtractor_133_out, subtractor_135_out, subtractor_136_out, subtractor_138_out, subtractor_140_out,
       subtractor_141_out, subtractor_143_out;

  Subtractor #(.width(7)) subtractor_1 (
    .a(INSTRUCTION[6:0]), .b(7'b1100111), .out(subtractor_1_out));  // open: bin, bout
  Subtractor #(.width(7)) subtractor_2 (
    .a(INSTRUCTION[6:0]), .b(7'b0000011), .out(subtractor_2_out));  // open: bin, bout
  Subtractor #(.width(7)) subtractor_3 (
    .a(INSTRUCTION[6:0]), .b(7'b0010011), .out(subtractor_3_out));  // open: bin, bout
  Subtractor #(.width(7)) subtractor_4 (
    .a(INSTRUCTION[6:0]), .b(7'b0100011), .out(subtractor_4_out));  // open: bin, bout
  Subtractor #(.width(7)) subtractor_5 (
    .a(INSTRUCTION[6:0]), .b(7'b0110111), .out(subtractor_5_out));  // open: bin, bout
  Subtractor #(.width(7)) subtractor_6 (
    .a(INSTRUCTION[6:0]), .b(7'b0110011), .out(subtractor_6_out));  // open: bin, bout
  Subtractor #(.width(7)) subtractor_7 (
    .a(INSTRUCTION[6:0]), .b(7'b0000011), .out(subtractor_7_out));  // open: bin, bout
  Subtractor #(.width(7)) subtractor_8 (
    .a(INSTRUCTION[6:0]), .b(7'b0010011), .out(subtractor_8_out));  // open: bin, bout
  Subtractor #(.width(7)) subtractor_9 (
    .a(INSTRUCTION[6:0]), .b(7'b1100111), .out(subtractor_9_out));  // open: bin, bout
  Subtractor #(.width(7)) subtractor_10 (
    .a(INSTRUCTION[6:0]), .b(7'b0110111), .out(subtractor_10_out));  // open: bin, bout
  Subtractor #(.width(7)) subtractor_11 (
    .a(INSTRUCTION[6:0]), .b(7'b1101111), .out(subtractor_11_out));  // open: bin, bout
  Subtractor #(.width(7)) subtractor_12 (
    .a(INSTRUCTION[6:0]), .b(7'b0100011), .out(subtractor_12_out));  // open: bin, bout
  Subtractor #(.width(7)) subtractor_13 (
    .a(INSTRUCTION[6:0]), .b(7'b0110111), .out(subtractor_13_out));  // open: bin, bout
  Subtractor #(.width(7)) subtractor_14 (
    .a(INSTRUCTION[6:0]), .b(7'b1100011), .out(subtractor_14_out));  // open: bin, bout
  Subtractor #(.width(7)) subtractor_15 (
    .a(INSTRUCTION[6:0]), .b(7'b0110111), .out(subtractor_15_out));  // open: bin, bout
  Subtractor #(.width(7)) subtractor_16 (
    .a(INSTRUCTION[6:0]), .b(7'b1101111), .out(subtractor_16_out));  // open: bin, bout
  Subtractor #(.width(7)) subtractor_17 (
    .a(INSTRUCTION[6:0]), .b(7'b1100011), .out(subtractor_17_out));  // open: bin, bout
  Subtractor #(.width(7)) subtractor_18 (
    .a(INSTRUCTION[6:0]), .b(7'b1101111), .out(subtractor_18_out));  // open: bin, bout
  Subtractor #(.width(7)) subtractor_19 (
    .a(INSTRUCTION[6:0]), .b(7'b1100111), .out(subtractor_19_out));  // open: bin, bout
  Subtractor #(.width(3)) subtractor_20 (
    .a(INSTRUCTION[14:12]), .b(3'b000), .out(subtractor_20_out));  // open: bin, bout
  not not_1 (not_1_out, subtractor_21_out[0]);
  Subtractor #(.width(3)) subtractor_21 (
    .a(INSTRUCTION[14:12]), .b(3'b001), .out(subtractor_21_out));  // open: bin, bout
  not not_2 (not_2_out, subtractor_21_out[1]);
  not not_3 (not_3_out, subtractor_21_out[2]);
  not not_4 (not_4_out, subtractor_22_out[0]);
  not not_5 (not_5_out, subtractor_22_out[1]);
  not not_6 (not_6_out, subtractor_22_out[2]);
  Subtractor #(.width(7)) subtractor_22 (
    .a(INSTRUCTION[6:0]), .b(7'b0000011), .out(subtractor_22_out));  // open: bin, bout
  not not_7 (not_7_out, subtractor_22_out[3]);
  not not_8 (not_8_out, subtractor_22_out[4]);
  not not_9 (not_9_out, subtractor_22_out[5]);
  not not_10 (not_10_out, subtractor_22_out[6]);
  not not_11 (not_11_out, subtractor_23_out[0]);
  not not_12 (not_12_out, subtractor_23_out[1]);
  Subtractor #(.width(3)) subtractor_23 (
    .a(INSTRUCTION[14:12]), .b(3'b000), .out(subtractor_23_out));  // open: bin, bout
  not not_13 (not_13_out, subtractor_23_out[2]);
  not not_14 (not_14_out, subtractor_24_out[0]);
  not not_15 (not_15_out, subtractor_24_out[1]);
  not not_16 (not_16_out, subtractor_24_out[2]);
  Subtractor #(.width(7)) subtractor_24 (
    .a(INSTRUCTION[6:0]), .b(7'b0000011), .out(subtractor_24_out));  // open: bin, bout
  not not_17 (not_17_out, subtractor_24_out[3]);
  not not_18 (not_18_out, subtractor_24_out[4]);
  not not_19 (not_19_out, subtractor_24_out[5]);
  not not_20 (not_20_out, subtractor_24_out[6]);
  not not_21 (not_21_out, subtractor_1_out[0]);
  not not_22 (not_22_out, subtractor_1_out[1]);
  not not_23 (not_23_out, subtractor_1_out[2]);
  not not_24 (not_24_out, subtractor_1_out[3]);
  not not_25 (not_25_out, subtractor_1_out[4]);
  not not_26 (not_26_out, subtractor_1_out[5]);
  not not_27 (not_27_out, subtractor_1_out[6]);
  not not_28 (not_28_out, subtractor_2_out[0]);
  not not_29 (not_29_out, subtractor_2_out[1]);
  not not_30 (not_30_out, subtractor_2_out[2]);
  not not_31 (not_31_out, subtractor_2_out[3]);
  not not_32 (not_32_out, subtractor_2_out[4]);
  not not_33 (not_33_out, subtractor_2_out[5]);
  not not_34 (not_34_out, subtractor_2_out[6]);
  not not_35 (not_35_out, subtractor_3_out[0]);
  not not_36 (not_36_out, subtractor_3_out[1]);
  not not_37 (not_37_out, subtractor_3_out[2]);
  not not_38 (not_38_out, subtractor_3_out[3]);
  not not_39 (not_39_out, subtractor_3_out[4]);
  not not_40 (not_40_out, subtractor_3_out[5]);
  not not_41 (not_41_out, subtractor_3_out[6]);
  not not_42 (not_42_out, subtractor_4_out[0]);
  not not_43 (not_43_out, subtractor_4_out[1]);
  not not_44 (not_44_out, subtractor_4_out[2]);
  not not_45 (not_45_out, subtractor_4_out[3]);
  not not_46 (not_46_out, subtractor_4_out[4]);
  not not_47 (not_47_out, subtractor_4_out[5]);
  not not_48 (not_48_out, subtractor_4_out[6]);
  not not_49 (not_49_out, subtractor_5_out[0]);
  not not_50 (not_50_out, subtractor_5_out[1]);
  not not_51 (not_51_out, subtractor_5_out[2]);
  not not_52 (not_52_out, subtractor_5_out[3]);
  not not_53 (not_53_out, subtractor_5_out[4]);
  not not_54 (not_54_out, subtractor_5_out[5]);
  not not_55 (not_55_out, subtractor_5_out[6]);
  not not_56 (not_56_out, subtractor_6_out[0]);
  not not_57 (not_57_out, subtractor_6_out[1]);
  not not_58 (not_58_out, subtractor_6_out[2]);
  not not_59 (not_59_out, subtractor_6_out[3]);
  not not_60 (not_60_out, subtractor_6_out[4]);
  not not_61 (not_61_out, subtractor_6_out[5]);
  not not_62 (not_62_out, subtractor_6_out[6]);
  not not_63 (not_63_out, subtractor_7_out[0]);
  not not_64 (not_64_out, subtractor_7_out[1]);
  not not_65 (not_65_out, subtractor_7_out[2]);
  not not_66 (not_66_out, subtractor_7_out[3]);
  not not_67 (not_67_out, subtractor_7_out[4]);
  not not_68 (not_68_out, subtractor_7_out[5]);
  not not_69 (not_69_out, subtractor_7_out[6]);
  not not_70 (not_70_out, subtractor_8_out[0]);
  not not_71 (not_71_out, subtractor_8_out[1]);
  not not_72 (not_72_out, subtractor_8_out[2]);
  not not_73 (not_73_out, subtractor_8_out[3]);
  not not_74 (not_74_out, subtractor_8_out[4]);
  not not_75 (not_75_out, subtractor_8_out[5]);
  not not_76 (not_76_out, subtractor_8_out[6]);
  not not_77 (not_77_out, subtractor_9_out[0]);
  not not_78 (not_78_out, subtractor_9_out[1]);
  not not_79 (not_79_out, subtractor_9_out[2]);
  not not_80 (not_80_out, subtractor_9_out[3]);
  not not_81 (not_81_out, subtractor_9_out[4]);
  not not_82 (not_82_out, subtractor_9_out[5]);
  not not_83 (not_83_out, subtractor_9_out[6]);
  not not_84 (not_84_out, subtractor_10_out[0]);
  not not_85 (not_85_out, subtractor_10_out[1]);
  not not_86 (not_86_out, subtractor_10_out[2]);
  not not_87 (not_87_out, subtractor_10_out[3]);
  not not_88 (not_88_out, subtractor_10_out[4]);
  not not_89 (not_89_out, subtractor_10_out[5]);
  not not_90 (not_90_out, subtractor_10_out[6]);
  not not_91 (not_91_out, subtractor_11_out[0]);
  not not_92 (not_92_out, subtractor_11_out[1]);
  not not_93 (not_93_out, subtractor_11_out[2]);
  not not_94 (not_94_out, subtractor_11_out[3]);
  not not_95 (not_95_out, subtractor_11_out[4]);
  not not_96 (not_96_out, subtractor_11_out[5]);
  not not_97 (not_97_out, subtractor_11_out[6]);
  not not_98 (not_98_out, subtractor_12_out[0]);
  not not_99 (not_99_out, subtractor_12_out[1]);
  not not_100 (not_100_out, subtractor_12_out[2]);
  not not_101 (not_101_out, subtractor_12_out[3]);
  not not_102 (not_102_out, subtractor_12_out[4]);
  not not_103 (not_103_out, subtractor_12_out[5]);
  not not_104 (not_104_out, subtractor_12_out[6]);
  not not_105 (not_105_out, subtractor_13_out[0]);
  not not_106 (not_106_out, subtractor_13_out[1]);
  not not_107 (not_107_out, subtractor_13_out[2]);
  not not_108 (not_108_out, subtractor_13_out[3]);
  not not_109 (not_109_out, subtractor_13_out[4]);
  not not_110 (not_110_out, subtractor_13_out[5]);
  not not_111 (not_111_out, subtractor_13_out[6]);
  not not_112 (not_112_out, subtractor_14_out[0]);
  not not_113 (not_113_out, subtractor_14_out[1]);
  not not_114 (not_114_out, subtractor_14_out[2]);
  not not_115 (not_115_out, subtractor_14_out[3]);
  not not_116 (not_116_out, subtractor_14_out[4]);
  not not_117 (not_117_out, subtractor_14_out[5]);
  not not_118 (not_118_out, subtractor_14_out[6]);
  not not_119 (not_119_out, subtractor_15_out[0]);
  not not_120 (not_120_out, subtractor_15_out[1]);
  not not_121 (not_121_out, subtractor_15_out[2]);
  not not_122 (not_122_out, subtractor_15_out[3]);
  not not_123 (not_123_out, subtractor_15_out[4]);
  not not_124 (not_124_out, subtractor_15_out[5]);
  not not_125 (not_125_out, subtractor_15_out[6]);
  not not_126 (not_126_out, subtractor_16_out[0]);
  not not_127 (not_127_out, subtractor_16_out[1]);
  not not_128 (not_128_out, subtractor_16_out[2]);
  not not_129 (not_129_out, subtractor_16_out[3]);
  not not_130 (not_130_out, subtractor_16_out[4]);
  not not_131 (not_131_out, subtractor_16_out[5]);
  not not_132 (not_132_out, subtractor_16_out[6]);
  not not_133 (not_133_out, subtractor_17_out[0]);
  not not_134 (not_134_out, subtractor_17_out[1]);
  not not_135 (not_135_out, subtractor_17_out[2]);
  not not_136 (not_136_out, subtractor_17_out[3]);
  not not_137 (not_137_out, subtractor_17_out[4]);
  not not_138 (not_138_out, subtractor_17_out[5]);
  not not_139 (not_139_out, subtractor_17_out[6]);
  not not_140 (not_140_out, subtractor_18_out[0]);
  not not_141 (not_141_out, subtractor_18_out[1]);
  not not_142 (not_142_out, subtractor_18_out[2]);
  not not_143 (not_143_out, subtractor_18_out[3]);
  not not_144 (not_144_out, subtractor_18_out[4]);
  not not_145 (not_145_out, subtractor_18_out[5]);
  not not_146 (not_146_out, subtractor_18_out[6]);
  not not_147 (not_147_out, subtractor_19_out[0]);
  not not_148 (not_148_out, subtractor_19_out[1]);
  not not_149 (not_149_out, subtractor_19_out[2]);
  not not_150 (not_150_out, subtractor_19_out[3]);
  not not_151 (not_151_out, subtractor_19_out[4]);
  not not_152 (not_152_out, subtractor_19_out[5]);
  not not_153 (not_153_out, subtractor_19_out[6]);
  not not_154 (not_154_out, subtractor_20_out[0]);
  not not_155 (not_155_out, subtractor_20_out[1]);
  not not_156 (not_156_out, subtractor_20_out[2]);
  and and_1 (and_1_out, not_1_out, not_2_out, not_3_out);
  and and_2 (and_2_out, not_4_out, not_5_out, not_6_out, not_7_out, not_8_out, not_9_out, not_10_out);
  and and_3 (and_3_out, not_11_out, not_12_out, not_13_out);
  and and_4 (and_4_out, not_14_out, not_15_out, not_16_out, not_17_out, not_18_out, not_19_out, not_20_out);
  and and_5 (and_5_out, not_21_out, not_22_out, not_23_out, not_24_out, not_25_out, not_26_out, not_27_out);
  and and_6 (and_6_out, not_28_out, not_29_out, not_30_out, not_31_out, not_32_out, not_33_out, not_34_out);
  and and_7 (and_7_out, not_35_out, not_36_out, not_37_out, not_38_out, not_39_out, not_40_out, not_41_out);
  and and_8 (and_8_out, not_42_out, not_43_out, not_44_out, not_45_out, not_46_out, not_47_out, not_48_out);
  and and_9 (and_9_out, not_49_out, not_50_out, not_51_out, not_52_out, not_53_out, not_54_out, not_55_out);
  and and_10 (and_10_out, not_56_out, not_57_out, not_58_out, not_59_out, not_60_out, not_61_out, not_62_out);
  and and_11 (and_11_out, not_63_out, not_64_out, not_65_out, not_66_out, not_67_out, not_68_out, not_69_out);
  and and_12 (and_12_out, not_70_out, not_71_out, not_72_out, not_73_out, not_74_out, not_75_out, not_76_out);
  and and_13 (and_13_out, not_77_out, not_78_out, not_79_out, not_80_out, not_81_out, not_82_out, not_83_out);
  and and_14 (and_14_out, not_84_out, not_85_out, not_86_out, not_87_out, not_88_out, not_89_out, not_90_out);
  and and_15 (and_15_out, not_91_out, not_92_out, not_93_out, not_94_out, not_95_out, not_96_out, not_97_out);
  and and_16 (and_16_out, not_98_out, not_99_out, not_100_out, not_101_out, not_102_out, not_103_out, not_104_out);
  and and_17 (and_17_out, not_105_out, not_106_out, not_107_out, not_108_out, not_109_out, not_110_out, not_111_out);
  and and_18 (and_18_out, not_112_out, not_113_out, not_114_out, not_115_out, not_116_out, not_117_out, not_118_out);
  and and_19 (and_19_out, not_119_out, not_120_out, not_121_out, not_122_out, not_123_out, not_124_out, not_125_out);
  and and_20 (ExtOp[2], not_126_out, not_127_out, not_128_out, not_129_out, not_130_out, not_131_out, not_132_out);
  and and_21 (nPCsel, not_133_out, not_134_out, not_135_out, not_136_out, not_137_out, not_138_out, not_139_out);
  and and_22 (and_22_out, not_140_out, not_141_out, not_142_out, not_143_out, not_144_out, not_145_out, not_146_out);
  and and_23 (and_23_out, not_147_out, not_148_out, not_149_out, not_150_out, not_151_out, not_152_out, not_153_out);
  and and_24 (and_24_out, not_154_out, not_155_out, not_156_out);
  and and_25 (LoadOp[0], and_1_out, and_2_out);
  and and_26 (LoadOp[1], and_3_out, and_4_out);
  or or_1 (ALUsrc, and_5_out, and_6_out, and_7_out, and_8_out, and_9_out);
  or or_2 (RegWr, and_10_out, and_11_out, and_12_out, and_13_out, and_14_out, and_15_out);
  or or_3 (ExtOp[0], and_16_out, and_17_out);
  or or_4 (ExtOp[1], and_18_out, and_19_out);
  or or_5 (jump, and_22_out, and_27_out);
  and and_27 (and_27_out, and_23_out, and_24_out);
  Subtractor #(.width(7)) subtractor_25 (
    .a(INSTRUCTION[6:0]), .b(7'b0100011), .out(subtractor_25_out));  // open: bin, bout
  Subtractor #(.width(7)) subtractor_26 (
    .a(INSTRUCTION[6:0]), .b(7'b0000011), .out(subtractor_26_out));  // open: bin, bout
  not not_157 (not_157_out, subtractor_25_out[0]);
  not not_158 (not_158_out, subtractor_25_out[1]);
  not not_159 (not_159_out, subtractor_25_out[2]);
  not not_160 (not_160_out, subtractor_25_out[3]);
  not not_161 (not_161_out, subtractor_25_out[4]);
  not not_162 (not_162_out, subtractor_25_out[5]);
  not not_163 (not_163_out, subtractor_25_out[6]);
  not not_164 (not_164_out, subtractor_26_out[0]);
  not not_165 (not_165_out, subtractor_26_out[1]);
  not not_166 (not_166_out, subtractor_26_out[2]);
  not not_167 (not_167_out, subtractor_26_out[3]);
  not not_168 (not_168_out, subtractor_26_out[4]);
  not not_169 (not_169_out, subtractor_26_out[5]);
  not not_170 (not_170_out, subtractor_26_out[6]);
  not not_171 (not_171_out, subtractor_27_out[0]);
  Subtractor #(.width(3)) subtractor_27 (
    .a(INSTRUCTION[14:12]), .b(3'b011), .out(subtractor_27_out));  // open: bin, bout
  not not_172 (not_172_out, subtractor_27_out[1]);
  not not_173 (not_173_out, subtractor_27_out[2]);
  not not_174 (not_174_out, subtractor_28_out[0]);
  not not_175 (not_175_out, subtractor_28_out[1]);
  not not_176 (not_176_out, subtractor_28_out[2]);
  Subtractor #(.width(7)) subtractor_28 (
    .a(INSTRUCTION[31:25]), .b(7'b0000001), .out(subtractor_28_out));  // open: bin, bout
  not not_177 (not_177_out, subtractor_28_out[3]);
  not not_178 (not_178_out, subtractor_28_out[4]);
  not not_179 (not_179_out, subtractor_28_out[5]);
  not not_180 (not_180_out, subtractor_28_out[6]);
  not not_181 (not_181_out, subtractor_29_out[0]);
  not not_182 (not_182_out, subtractor_29_out[1]);
  not not_183 (not_183_out, subtractor_29_out[2]);
  Subtractor #(.width(7)) subtractor_29 (
    .a(INSTRUCTION[6:0]), .b(7'b0110011), .out(subtractor_29_out));  // open: bin, bout
  not not_184 (not_184_out, subtractor_29_out[3]);
  not not_185 (not_185_out, subtractor_29_out[4]);
  not not_186 (not_186_out, subtractor_29_out[5]);
  not not_187 (not_187_out, subtractor_29_out[6]);
  not not_188 (not_188_out, subtractor_30_out[0]);
  not not_189 (not_189_out, subtractor_30_out[1]);
  Subtractor #(.width(3)) subtractor_30 (
    .a(INSTRUCTION[14:12]), .b(3'b010), .out(subtractor_30_out));  // open: bin, bout
  not not_190 (not_190_out, subtractor_30_out[2]);
  not not_191 (not_191_out, subtractor_31_out[0]);
  not not_192 (not_192_out, subtractor_31_out[1]);
  not not_193 (not_193_out, subtractor_31_out[2]);
  not not_194 (not_194_out, subtractor_31_out[3]);
  Subtractor #(.width(7)) subtractor_31 (
    .a(INSTRUCTION[31:25]), .b({7{1'b0}}), .out(subtractor_31_out));  // open: bin, bout
  not not_195 (not_195_out, subtractor_31_out[4]);
  not not_196 (not_196_out, subtractor_31_out[5]);
  not not_197 (not_197_out, subtractor_31_out[6]);
  not not_198 (not_198_out, subtractor_32_out[0]);
  not not_199 (not_199_out, subtractor_32_out[1]);
  not not_200 (not_200_out, subtractor_32_out[2]);
  not not_201 (not_201_out, subtractor_32_out[3]);
  Subtractor #(.width(7)) subtractor_32 (
    .a(INSTRUCTION[6:0]), .b(7'b0110011), .out(subtractor_32_out));  // open: bin, bout
  not not_202 (not_202_out, subtractor_32_out[4]);
  not not_203 (not_203_out, subtractor_32_out[5]);
  not not_204 (not_204_out, subtractor_32_out[6]);
  not not_205 (not_205_out, subtractor_33_out[0]);
  not not_206 (not_206_out, subtractor_33_out[1]);
  Subtractor #(.width(3)) subtractor_33 (
    .a(INSTRUCTION[14:12]), .b(3'b100), .out(subtractor_33_out));  // open: bin, bout
  not not_207 (not_207_out, subtractor_33_out[2]);
  not not_208 (not_208_out, subtractor_34_out[0]);
  not not_209 (not_209_out, subtractor_34_out[1]);
  not not_210 (not_210_out, subtractor_34_out[2]);
  not not_211 (not_211_out, subtractor_34_out[3]);
  Subtractor #(.width(7)) subtractor_34 (
    .a(INSTRUCTION[31:25]), .b({7{1'b0}}), .out(subtractor_34_out));  // open: bin, bout
  not not_212 (not_212_out, subtractor_34_out[4]);
  not not_213 (not_213_out, subtractor_34_out[5]);
  not not_214 (not_214_out, subtractor_34_out[6]);
  not not_215 (not_215_out, subtractor_35_out[0]);
  not not_216 (not_216_out, subtractor_35_out[1]);
  not not_217 (not_217_out, subtractor_35_out[2]);
  Subtractor #(.width(7)) subtractor_35 (
    .a(INSTRUCTION[6:0]), .b(7'b0110011), .out(subtractor_35_out));  // open: bin, bout
  not not_218 (not_218_out, subtractor_35_out[3]);
  not not_219 (not_219_out, subtractor_35_out[4]);
  not not_220 (not_220_out, subtractor_35_out[5]);
  not not_221 (not_221_out, subtractor_35_out[6]);
  not not_222 (not_222_out, subtractor_36_out[0]);
  not not_223 (not_223_out, subtractor_36_out[1]);
  Subtractor #(.width(3)) subtractor_36 (
    .a(INSTRUCTION[14:12]), .b(3'b111), .out(subtractor_36_out));  // open: bin, bout
  not not_224 (not_224_out, subtractor_36_out[2]);
  not not_225 (not_225_out, subtractor_37_out[0]);
  not not_226 (not_226_out, subtractor_37_out[1]);
  not not_227 (not_227_out, subtractor_37_out[2]);
  Subtractor #(.width(7)) subtractor_37 (
    .a(INSTRUCTION[31:25]), .b(7'b0000001), .out(subtractor_37_out));  // open: bin, bout
  not not_228 (not_228_out, subtractor_37_out[3]);
  not not_229 (not_229_out, subtractor_37_out[4]);
  not not_230 (not_230_out, subtractor_37_out[5]);
  not not_231 (not_231_out, subtractor_37_out[6]);
  not not_232 (not_232_out, subtractor_38_out[0]);
  not not_233 (not_233_out, subtractor_38_out[1]);
  not not_234 (not_234_out, subtractor_38_out[2]);
  not not_235 (not_235_out, subtractor_38_out[3]);
  Subtractor #(.width(7)) subtractor_38 (
    .a(INSTRUCTION[6:0]), .b(7'b0110011), .out(subtractor_38_out));  // open: bin, bout
  not not_236 (not_236_out, subtractor_38_out[4]);
  not not_237 (not_237_out, subtractor_38_out[5]);
  not not_238 (not_238_out, subtractor_38_out[6]);
  not not_239 (not_239_out, subtractor_39_out[0]);
  not not_240 (not_240_out, subtractor_39_out[1]);
  Subtractor #(.width(3)) subtractor_39 (
    .a(INSTRUCTION[14:12]), .b(3'b111), .out(subtractor_39_out));  // open: bin, bout
  not not_241 (not_241_out, subtractor_39_out[2]);
  not not_242 (not_242_out, subtractor_40_out[0]);
  not not_243 (not_243_out, subtractor_40_out[1]);
  not not_244 (not_244_out, subtractor_40_out[2]);
  Subtractor #(.width(7)) subtractor_40 (
    .a(INSTRUCTION[31:25]), .b({7{1'b0}}), .out(subtractor_40_out));  // open: bin, bout
  not not_245 (not_245_out, subtractor_40_out[3]);
  not not_246 (not_246_out, subtractor_40_out[4]);
  not not_247 (not_247_out, subtractor_40_out[5]);
  not not_248 (not_248_out, subtractor_40_out[6]);
  not not_249 (not_249_out, subtractor_41_out[0]);
  not not_250 (not_250_out, subtractor_41_out[1]);
  not not_251 (not_251_out, subtractor_41_out[2]);
  not not_252 (not_252_out, subtractor_41_out[3]);
  Subtractor #(.width(7)) subtractor_41 (
    .a(INSTRUCTION[6:0]), .b(7'b0110011), .out(subtractor_41_out));  // open: bin, bout
  not not_253 (not_253_out, subtractor_41_out[4]);
  not not_254 (not_254_out, subtractor_41_out[5]);
  not not_255 (not_255_out, subtractor_41_out[6]);
  not not_256 (not_256_out, subtractor_42_out[0]);
  not not_257 (not_257_out, subtractor_42_out[1]);
  Subtractor #(.width(3)) subtractor_42 (
    .a(INSTRUCTION[14:12]), .b(3'b010), .out(subtractor_42_out));  // open: bin, bout
  not not_258 (not_258_out, subtractor_42_out[2]);
  not not_259 (not_259_out, subtractor_43_out[0]);
  not not_260 (not_260_out, subtractor_43_out[1]);
  not not_261 (not_261_out, subtractor_43_out[2]);
  Subtractor #(.width(7)) subtractor_43 (
    .a(INSTRUCTION[6:0]), .b(7'b0010011), .out(subtractor_43_out));  // open: bin, bout
  not not_262 (not_262_out, subtractor_43_out[3]);
  not not_263 (not_263_out, subtractor_43_out[4]);
  not not_264 (not_264_out, subtractor_43_out[5]);
  not not_265 (not_265_out, subtractor_43_out[6]);
  not not_266 (not_266_out, subtractor_44_out[0]);
  not not_267 (not_267_out, subtractor_44_out[1]);
  Subtractor #(.width(3)) subtractor_44 (
    .a(INSTRUCTION[14:12]), .b(3'b100), .out(subtractor_44_out));  // open: bin, bout
  not not_268 (not_268_out, subtractor_44_out[2]);
  not not_269 (not_269_out, subtractor_45_out[0]);
  not not_270 (not_270_out, subtractor_45_out[1]);
  not not_271 (not_271_out, subtractor_45_out[2]);
  Subtractor #(.width(7)) subtractor_45 (
    .a(INSTRUCTION[6:0]), .b(7'b0010011), .out(subtractor_45_out));  // open: bin, bout
  not not_272 (not_272_out, subtractor_45_out[3]);
  not not_273 (not_273_out, subtractor_45_out[4]);
  not not_274 (not_274_out, subtractor_45_out[5]);
  not not_275 (not_275_out, subtractor_45_out[6]);
  not not_276 (not_276_out, subtractor_46_out[0]);
  not not_277 (not_277_out, subtractor_46_out[1]);
  Subtractor #(.width(3)) subtractor_46 (
    .a(INSTRUCTION[14:12]), .b(3'b101), .out(subtractor_46_out));  // open: bin, bout
  not not_278 (not_278_out, subtractor_46_out[2]);
  not not_279 (not_279_out, subtractor_47_out[0]);
  not not_280 (not_280_out, subtractor_47_out[1]);
  not not_281 (not_281_out, subtractor_47_out[2]);
  not not_282 (not_282_out, subtractor_47_out[3]);
  Subtractor #(.width(7)) subtractor_47 (
    .a(INSTRUCTION[31:25]), .b(7'b0100000), .out(subtractor_47_out));  // open: bin, bout
  not not_283 (not_283_out, subtractor_47_out[4]);
  not not_284 (not_284_out, subtractor_47_out[5]);
  not not_285 (not_285_out, subtractor_47_out[6]);
  not not_286 (not_286_out, subtractor_48_out[0]);
  not not_287 (not_287_out, subtractor_48_out[1]);
  not not_288 (not_288_out, subtractor_48_out[2]);
  not not_289 (not_289_out, subtractor_48_out[3]);
  Subtractor #(.width(7)) subtractor_48 (
    .a(INSTRUCTION[6:0]), .b(7'b0010011), .out(subtractor_48_out));  // open: bin, bout
  not not_290 (not_290_out, subtractor_48_out[4]);
  not not_291 (not_291_out, subtractor_48_out[5]);
  not not_292 (not_292_out, subtractor_48_out[6]);
  not not_293 (not_293_out, subtractor_49_out[0]);
  Subtractor #(.width(3)) subtractor_49 (
    .a(INSTRUCTION[14:12]), .b(3'b111), .out(subtractor_49_out));  // open: bin, bout
  not not_294 (not_294_out, subtractor_49_out[1]);
  not not_295 (not_295_out, subtractor_49_out[2]);
  not not_296 (not_296_out, subtractor_50_out[0]);
  not not_297 (not_297_out, subtractor_50_out[1]);
  not not_298 (not_298_out, subtractor_50_out[2]);
  not not_299 (not_299_out, subtractor_50_out[3]);
  Subtractor #(.width(7)) subtractor_50 (
    .a(INSTRUCTION[6:0]), .b(7'b0010011), .out(subtractor_50_out));  // open: bin, bout
  not not_300 (not_300_out, subtractor_50_out[4]);
  not not_301 (not_301_out, subtractor_50_out[5]);
  not not_302 (not_302_out, subtractor_50_out[6]);
  not not_303 (not_303_out, subtractor_51_out[0]);
  not not_304 (not_304_out, subtractor_51_out[1]);
  Subtractor #(.width(3)) subtractor_51 (
    .a(INSTRUCTION[14:12]), .b(3'b100), .out(subtractor_51_out));  // open: bin, bout
  not not_305 (not_305_out, subtractor_51_out[2]);
  not not_306 (not_306_out, subtractor_52_out[0]);
  not not_307 (not_307_out, subtractor_52_out[1]);
  not not_308 (not_308_out, subtractor_52_out[2]);
  Subtractor #(.width(7)) subtractor_52 (
    .a(INSTRUCTION[6:0]), .b(7'b1100011), .out(subtractor_52_out));  // open: bin, bout
  not not_309 (not_309_out, subtractor_52_out[3]);
  not not_310 (not_310_out, subtractor_52_out[4]);
  not not_311 (not_311_out, subtractor_52_out[5]);
  not not_312 (not_312_out, subtractor_52_out[6]);
  not not_313 (not_313_out, subtractor_53_out[0]);
  not not_314 (not_314_out, subtractor_53_out[1]);
  not not_315 (not_315_out, subtractor_53_out[2]);
  Subtractor #(.width(7)) subtractor_53 (
    .a(INSTRUCTION[6:0]), .b(7'b0110111), .out(subtractor_53_out));  // open: bin, bout
  not not_316 (not_316_out, subtractor_53_out[3]);
  not not_317 (not_317_out, subtractor_53_out[4]);
  not not_318 (not_318_out, subtractor_53_out[5]);
  not not_319 (not_319_out, subtractor_53_out[6]);
  and and_28 (MemWr, not_157_out, not_158_out, not_159_out, not_160_out, not_161_out, not_162_out, not_163_out);
  and and_29 (MemtoReg, not_164_out, not_165_out, not_166_out, not_167_out, not_168_out, not_169_out, not_170_out);
  and and_30 (and_30_out, not_171_out, not_172_out, not_173_out);
  and and_31 (and_31_out, not_174_out, not_175_out, not_176_out, not_177_out, not_178_out, not_179_out, not_180_out);
  and and_32 (and_32_out, not_181_out, not_182_out, not_183_out, not_184_out, not_185_out, not_186_out, not_187_out);
  and and_33 (and_33_out, not_188_out, not_189_out, not_190_out);
  and and_34 (and_34_out, not_191_out, not_192_out, not_193_out, not_194_out, not_195_out, not_196_out, not_197_out);
  and and_35 (and_35_out, not_198_out, not_199_out, not_200_out, not_201_out, not_202_out, not_203_out, not_204_out);
  and and_36 (and_36_out, not_205_out, not_206_out, not_207_out);
  and and_37 (and_37_out, not_208_out, not_209_out, not_210_out, not_211_out, not_212_out, not_213_out, not_214_out);
  and and_38 (and_38_out, not_215_out, not_216_out, not_217_out, not_218_out, not_219_out, not_220_out, not_221_out);
  and and_39 (and_39_out, not_222_out, not_223_out, not_224_out);
  and and_40 (and_40_out, not_225_out, not_226_out, not_227_out, not_228_out, not_229_out, not_230_out, not_231_out);
  and and_41 (and_41_out, not_232_out, not_233_out, not_234_out, not_235_out, not_236_out, not_237_out, not_238_out);
  and and_42 (and_42_out, not_239_out, not_240_out, not_241_out);
  and and_43 (and_43_out, not_242_out, not_243_out, not_244_out, not_245_out, not_246_out, not_247_out, not_248_out);
  and and_44 (and_44_out, not_249_out, not_250_out, not_251_out, not_252_out, not_253_out, not_254_out, not_255_out);
  and and_45 (and_45_out, not_256_out, not_257_out, not_258_out);
  and and_46 (and_46_out, not_259_out, not_260_out, not_261_out, not_262_out, not_263_out, not_264_out, not_265_out);
  and and_47 (and_47_out, not_266_out, not_267_out, not_268_out);
  and and_48 (and_48_out, not_269_out, not_270_out, not_271_out, not_272_out, not_273_out, not_274_out, not_275_out);
  and and_49 (and_49_out, not_276_out, not_277_out, not_278_out);
  and and_50 (and_50_out, not_279_out, not_280_out, not_281_out, not_282_out, not_283_out, not_284_out, not_285_out);
  and and_51 (and_51_out, not_286_out, not_287_out, not_288_out, not_289_out, not_290_out, not_291_out, not_292_out);
  and and_52 (and_52_out, not_293_out, not_294_out, not_295_out);
  and and_53 (and_53_out, not_296_out, not_297_out, not_298_out, not_299_out, not_300_out, not_301_out, not_302_out);
  and and_54 (and_54_out, not_303_out, not_304_out, not_305_out);
  and and_55 (and_55_out, not_306_out, not_307_out, not_308_out, not_309_out, not_310_out, not_311_out, not_312_out);
  and and_56 (and_56_out, not_313_out, not_314_out, not_315_out, not_316_out, not_317_out, not_318_out, not_319_out);
  and and_57 (and_57_out, and_30_out, and_31_out, and_32_out);
  and and_58 (and_58_out, and_33_out, and_34_out, and_35_out);
  and and_59 (and_59_out, and_36_out, and_37_out, and_38_out);
  and and_60 (and_60_out, and_39_out, and_40_out, and_41_out);
  and and_61 (and_61_out, and_42_out, and_43_out, and_44_out);
  and and_62 (and_62_out, and_45_out, and_46_out);
  and and_63 (and_63_out, and_47_out, and_48_out);
  and and_64 (and_64_out, and_49_out, and_50_out, and_51_out);
  and and_65 (and_65_out, and_52_out, and_53_out);
  and and_66 (and_66_out, and_54_out, and_55_out);
  or or_6 (ALUctr[0], and_57_out, and_58_out, and_59_out, and_60_out, and_61_out, and_62_out, and_63_out, and_64_out, and_65_out, and_66_out, and_56_out);
  Subtractor #(.width(7)) subtractor_54 (
    .a(INSTRUCTION[31:25]), .b(7'b0000001), .out(subtractor_54_out));  // open: bin, bout
  Subtractor #(.width(7)) subtractor_55 (
    .a(INSTRUCTION[6:0]), .b(7'b0110011), .out(subtractor_55_out));  // open: bin, bout
  Subtractor #(.width(7)) subtractor_56 (
    .a(INSTRUCTION[31:25]), .b({7{1'b0}}), .out(subtractor_56_out));  // open: bin, bout
  Subtractor #(.width(7)) subtractor_57 (
    .a(INSTRUCTION[6:0]), .b(7'b0110011), .out(subtractor_57_out));  // open: bin, bout
  Subtractor #(.width(7)) subtractor_58 (
    .a(INSTRUCTION[31:25]), .b(7'b0000001), .out(subtractor_58_out));  // open: bin, bout
  Subtractor #(.width(7)) subtractor_59 (
    .a(INSTRUCTION[6:0]), .b(7'b0110011), .out(subtractor_59_out));  // open: bin, bout
  Subtractor #(.width(7)) subtractor_60 (
    .a(INSTRUCTION[31:25]), .b(7'b0000001), .out(subtractor_60_out));  // open: bin, bout
  Subtractor #(.width(7)) subtractor_61 (
    .a(INSTRUCTION[6:0]), .b(7'b0110011), .out(subtractor_61_out));  // open: bin, bout
  Subtractor #(.width(7)) subtractor_62 (
    .a(INSTRUCTION[31:25]), .b({7{1'b0}}), .out(subtractor_62_out));  // open: bin, bout
  Subtractor #(.width(7)) subtractor_63 (
    .a(INSTRUCTION[6:0]), .b(7'b0110011), .out(subtractor_63_out));  // open: bin, bout
  Subtractor #(.width(7)) subtractor_64 (
    .a(INSTRUCTION[31:25]), .b({7{1'b0}}), .out(subtractor_64_out));  // open: bin, bout
  Subtractor #(.width(7)) subtractor_65 (
    .a(INSTRUCTION[6:0]), .b(7'b0110011), .out(subtractor_65_out));  // open: bin, bout
  Subtractor #(.width(7)) subtractor_66 (
    .a(INSTRUCTION[31:25]), .b({7{1'b0}}), .out(subtractor_66_out));  // open: bin, bout
  Subtractor #(.width(7)) subtractor_67 (
    .a(INSTRUCTION[6:0]), .b(7'b0110011), .out(subtractor_67_out));  // open: bin, bout
  Subtractor #(.width(3)) subtractor_68 (
    .a(INSTRUCTION[14:12]), .b(3'b001), .out(subtractor_68_out));  // open: bin, bout
  Subtractor #(.width(7)) subtractor_69 (
    .a(INSTRUCTION[31:25]), .b({7{1'b0}}), .out(subtractor_69_out));  // open: bin, bout
  Subtractor #(.width(7)) subtractor_70 (
    .a(INSTRUCTION[6:0]), .b(7'b0010011), .out(subtractor_70_out));  // open: bin, bout
  Subtractor #(.width(3)) subtractor_71 (
    .a(INSTRUCTION[14:12]), .b(3'b010), .out(subtractor_71_out));  // open: bin, bout
  Subtractor #(.width(7)) subtractor_72 (
    .a(INSTRUCTION[6:0]), .b(7'b0010011), .out(subtractor_72_out));  // open: bin, bout
  Subtractor #(.width(3)) subtractor_73 (
    .a(INSTRUCTION[14:12]), .b(3'b100), .out(subtractor_73_out));  // open: bin, bout
  Subtractor #(.width(7)) subtractor_74 (
    .a(INSTRUCTION[6:0]), .b(7'b0010011), .out(subtractor_74_out));  // open: bin, bout
  Subtractor #(.width(3)) subtractor_75 (
    .a(INSTRUCTION[14:12]), .b(3'b110), .out(subtractor_75_out));  // open: bin, bout
  Subtractor #(.width(7)) subtractor_76 (
    .a(INSTRUCTION[6:0]), .b(7'b0010011), .out(subtractor_76_out));  // open: bin, bout
  Subtractor #(.width(3)) subtractor_77 (
    .a(INSTRUCTION[14:12]), .b(3'b100), .out(subtractor_77_out));  // open: bin, bout
  Subtractor #(.width(7)) subtractor_78 (
    .a(INSTRUCTION[6:0]), .b(7'b1100011), .out(subtractor_78_out));  // open: bin, bout
  not not_320 (not_320_out, subtractor_79_out[0]);
  Subtractor #(.width(3)) subtractor_79 (
    .a(INSTRUCTION[14:12]), .b(3'b000), .out(subtractor_79_out));  // open: bin, bout
  not not_321 (not_321_out, subtractor_79_out[1]);
  not not_322 (not_322_out, subtractor_79_out[2]);
  not not_323 (not_323_out, subtractor_54_out[0]);
  not not_324 (not_324_out, subtractor_54_out[1]);
  not not_325 (not_325_out, subtractor_54_out[2]);
  not not_326 (not_326_out, subtractor_54_out[3]);
  not not_327 (not_327_out, subtractor_54_out[4]);
  not not_328 (not_328_out, subtractor_54_out[5]);
  not not_329 (not_329_out, subtractor_54_out[6]);
  not not_330 (not_330_out, subtractor_55_out[0]);
  not not_331 (not_331_out, subtractor_55_out[1]);
  not not_332 (not_332_out, subtractor_55_out[2]);
  not not_333 (not_333_out, subtractor_55_out[3]);
  not not_334 (not_334_out, subtractor_55_out[4]);
  not not_335 (not_335_out, subtractor_55_out[5]);
  not not_336 (not_336_out, subtractor_55_out[6]);
  not not_337 (not_337_out, subtractor_80_out[0]);
  Subtractor #(.width(3)) subtractor_80 (
    .a(INSTRUCTION[14:12]), .b(3'b001), .out(subtractor_80_out));  // open: bin, bout
  not not_338 (not_338_out, subtractor_80_out[1]);
  not not_339 (not_339_out, subtractor_80_out[2]);
  not not_340 (not_340_out, subtractor_56_out[0]);
  not not_341 (not_341_out, subtractor_56_out[1]);
  not not_342 (not_342_out, subtractor_56_out[2]);
  not not_343 (not_343_out, subtractor_56_out[3]);
  not not_344 (not_344_out, subtractor_56_out[4]);
  not not_345 (not_345_out, subtractor_56_out[5]);
  not not_346 (not_346_out, subtractor_56_out[6]);
  not not_347 (not_347_out, subtractor_57_out[0]);
  not not_348 (not_348_out, subtractor_57_out[1]);
  not not_349 (not_349_out, subtractor_57_out[2]);
  not not_350 (not_350_out, subtractor_57_out[3]);
  not not_351 (not_351_out, subtractor_57_out[4]);
  not not_352 (not_352_out, subtractor_57_out[5]);
  not not_353 (not_353_out, subtractor_57_out[6]);
  not not_354 (not_354_out, subtractor_81_out[0]);
  not not_355 (not_355_out, subtractor_81_out[1]);
  Subtractor #(.width(3)) subtractor_81 (
    .a(INSTRUCTION[14:12]), .b(3'b001), .out(subtractor_81_out));  // open: bin, bout
  not not_356 (not_356_out, subtractor_81_out[2]);
  not not_357 (not_357_out, subtractor_58_out[0]);
  not not_358 (not_358_out, subtractor_58_out[1]);
  not not_359 (not_359_out, subtractor_58_out[2]);
  not not_360 (not_360_out, subtractor_58_out[3]);
  not not_361 (not_361_out, subtractor_58_out[4]);
  not not_362 (not_362_out, subtractor_58_out[5]);
  not not_363 (not_363_out, subtractor_58_out[6]);
  not not_364 (not_364_out, subtractor_59_out[0]);
  not not_365 (not_365_out, subtractor_59_out[1]);
  not not_366 (not_366_out, subtractor_59_out[2]);
  not not_367 (not_367_out, subtractor_59_out[3]);
  not not_368 (not_368_out, subtractor_59_out[4]);
  not not_369 (not_369_out, subtractor_59_out[5]);
  not not_370 (not_370_out, subtractor_59_out[6]);
  not not_371 (not_371_out, subtractor_82_out[0]);
  Subtractor #(.width(3)) subtractor_82 (
    .a(INSTRUCTION[14:12]), .b(3'b011), .out(subtractor_82_out));  // open: bin, bout
  not not_372 (not_372_out, subtractor_82_out[1]);
  not not_373 (not_373_out, subtractor_82_out[2]);
  not not_374 (not_374_out, subtractor_60_out[0]);
  not not_375 (not_375_out, subtractor_60_out[1]);
  not not_376 (not_376_out, subtractor_60_out[2]);
  not not_377 (not_377_out, subtractor_60_out[3]);
  not not_378 (not_378_out, subtractor_60_out[4]);
  not not_379 (not_379_out, subtractor_60_out[5]);
  not not_380 (not_380_out, subtractor_60_out[6]);
  not not_381 (not_381_out, subtractor_61_out[0]);
  not not_382 (not_382_out, subtractor_61_out[1]);
  not not_383 (not_383_out, subtractor_61_out[2]);
  not not_384 (not_384_out, subtractor_61_out[3]);
  not not_385 (not_385_out, subtractor_61_out[4]);
  not not_386 (not_386_out, subtractor_61_out[5]);
  not not_387 (not_387_out, subtractor_61_out[6]);
  not not_388 (not_388_out, subtractor_83_out[0]);
  Subtractor #(.width(3)) subtractor_83 (
    .a(INSTRUCTION[14:12]), .b(3'b010), .out(subtractor_83_out));  // open: bin, bout
  not not_389 (not_389_out, subtractor_83_out[1]);
  not not_390 (not_390_out, subtractor_83_out[2]);
  not not_391 (not_391_out, subtractor_62_out[0]);
  not not_392 (not_392_out, subtractor_62_out[1]);
  not not_393 (not_393_out, subtractor_62_out[2]);
  not not_394 (not_394_out, subtractor_62_out[3]);
  not not_395 (not_395_out, subtractor_62_out[4]);
  not not_396 (not_396_out, subtractor_62_out[5]);
  not not_397 (not_397_out, subtractor_62_out[6]);
  not not_398 (not_398_out, subtractor_63_out[0]);
  not not_399 (not_399_out, subtractor_63_out[1]);
  not not_400 (not_400_out, subtractor_63_out[2]);
  not not_401 (not_401_out, subtractor_63_out[3]);
  not not_402 (not_402_out, subtractor_63_out[4]);
  not not_403 (not_403_out, subtractor_63_out[5]);
  not not_404 (not_404_out, subtractor_63_out[6]);
  not not_405 (not_405_out, subtractor_84_out[0]);
  Subtractor #(.width(3)) subtractor_84 (
    .a(INSTRUCTION[14:12]), .b(3'b100), .out(subtractor_84_out));  // open: bin, bout
  not not_406 (not_406_out, subtractor_84_out[1]);
  not not_407 (not_407_out, subtractor_84_out[2]);
  not not_408 (not_408_out, subtractor_64_out[0]);
  not not_409 (not_409_out, subtractor_64_out[1]);
  not not_410 (not_410_out, subtractor_64_out[2]);
  not not_411 (not_411_out, subtractor_64_out[3]);
  not not_412 (not_412_out, subtractor_64_out[4]);
  not not_413 (not_413_out, subtractor_64_out[5]);
  not not_414 (not_414_out, subtractor_64_out[6]);
  not not_415 (not_415_out, subtractor_65_out[0]);
  not not_416 (not_416_out, subtractor_65_out[1]);
  not not_417 (not_417_out, subtractor_65_out[2]);
  not not_418 (not_418_out, subtractor_65_out[3]);
  not not_419 (not_419_out, subtractor_65_out[4]);
  not not_420 (not_420_out, subtractor_65_out[5]);
  not not_421 (not_421_out, subtractor_65_out[6]);
  not not_422 (not_422_out, subtractor_85_out[0]);
  not not_423 (not_423_out, subtractor_85_out[1]);
  Subtractor #(.width(3)) subtractor_85 (
    .a(INSTRUCTION[14:12]), .b(3'b110), .out(subtractor_85_out));  // open: bin, bout
  not not_424 (not_424_out, subtractor_85_out[2]);
  not not_425 (not_425_out, subtractor_66_out[0]);
  not not_426 (not_426_out, subtractor_66_out[1]);
  not not_427 (not_427_out, subtractor_66_out[2]);
  not not_428 (not_428_out, subtractor_66_out[3]);
  not not_429 (not_429_out, subtractor_66_out[4]);
  not not_430 (not_430_out, subtractor_66_out[5]);
  not not_431 (not_431_out, subtractor_66_out[6]);
  not not_432 (not_432_out, subtractor_67_out[0]);
  not not_433 (not_433_out, subtractor_67_out[1]);
  not not_434 (not_434_out, subtractor_67_out[2]);
  not not_435 (not_435_out, subtractor_67_out[3]);
  not not_436 (not_436_out, subtractor_67_out[4]);
  not not_437 (not_437_out, subtractor_67_out[5]);
  not not_438 (not_438_out, subtractor_67_out[6]);
  not not_439 (not_439_out, subtractor_68_out[0]);
  not not_440 (not_440_out, subtractor_68_out[1]);
  not not_441 (not_441_out, subtractor_68_out[2]);
  not not_442 (not_442_out, subtractor_69_out[0]);
  not not_443 (not_443_out, subtractor_69_out[1]);
  not not_444 (not_444_out, subtractor_69_out[2]);
  not not_445 (not_445_out, subtractor_69_out[3]);
  not not_446 (not_446_out, subtractor_69_out[4]);
  not not_447 (not_447_out, subtractor_69_out[5]);
  not not_448 (not_448_out, subtractor_69_out[6]);
  not not_449 (not_449_out, subtractor_70_out[0]);
  not not_450 (not_450_out, subtractor_70_out[1]);
  not not_451 (not_451_out, subtractor_70_out[2]);
  not not_452 (not_452_out, subtractor_70_out[3]);
  not not_453 (not_453_out, subtractor_70_out[4]);
  not not_454 (not_454_out, subtractor_70_out[5]);
  not not_455 (not_455_out, subtractor_70_out[6]);
  not not_456 (not_456_out, subtractor_71_out[0]);
  not not_457 (not_457_out, subtractor_71_out[1]);
  not not_458 (not_458_out, subtractor_71_out[2]);
  not not_459 (not_459_out, subtractor_72_out[0]);
  not not_460 (not_460_out, subtractor_72_out[1]);
  not not_461 (not_461_out, subtractor_72_out[2]);
  not not_462 (not_462_out, subtractor_72_out[3]);
  not not_463 (not_463_out, subtractor_72_out[4]);
  not not_464 (not_464_out, subtractor_72_out[5]);
  not not_465 (not_465_out, subtractor_72_out[6]);
  not not_466 (not_466_out, subtractor_73_out[0]);
  not not_467 (not_467_out, subtractor_73_out[1]);
  not not_468 (not_468_out, subtractor_73_out[2]);
  not not_469 (not_469_out, subtractor_74_out[0]);
  not not_470 (not_470_out, subtractor_74_out[1]);
  not not_471 (not_471_out, subtractor_74_out[2]);
  not not_472 (not_472_out, subtractor_74_out[3]);
  not not_473 (not_473_out, subtractor_74_out[4]);
  not not_474 (not_474_out, subtractor_74_out[5]);
  not not_475 (not_475_out, subtractor_74_out[6]);
  not not_476 (not_476_out, subtractor_75_out[0]);
  not not_477 (not_477_out, subtractor_75_out[1]);
  not not_478 (not_478_out, subtractor_75_out[2]);
  not not_479 (not_479_out, subtractor_76_out[0]);
  not not_480 (not_480_out, subtractor_76_out[1]);
  not not_481 (not_481_out, subtractor_76_out[2]);
  not not_482 (not_482_out, subtractor_76_out[3]);
  not not_483 (not_483_out, subtractor_76_out[4]);
  not not_484 (not_484_out, subtractor_76_out[5]);
  not not_485 (not_485_out, subtractor_76_out[6]);
  not not_486 (not_486_out, subtractor_77_out[0]);
  not not_487 (not_487_out, subtractor_77_out[1]);
  not not_488 (not_488_out, subtractor_77_out[2]);
  not not_489 (not_489_out, subtractor_78_out[0]);
  not not_490 (not_490_out, subtractor_78_out[1]);
  not not_491 (not_491_out, subtractor_78_out[2]);
  not not_492 (not_492_out, subtractor_78_out[3]);
  not not_493 (not_493_out, subtractor_78_out[4]);
  not not_494 (not_494_out, subtractor_78_out[5]);
  not not_495 (not_495_out, subtractor_78_out[6]);
  and and_67 (and_67_out, not_320_out, not_321_out, not_322_out);
  and and_68 (and_68_out, not_323_out, not_324_out, not_325_out, not_326_out, not_327_out, not_328_out, not_329_out);
  and and_69 (and_69_out, not_330_out, not_331_out, not_332_out, not_333_out, not_334_out, not_335_out, not_336_out);
  and and_70 (and_70_out, not_337_out, not_338_out, not_339_out);
  and and_71 (and_71_out, not_340_out, not_341_out, not_342_out, not_343_out, not_344_out, not_345_out, not_346_out);
  and and_72 (and_72_out, not_347_out, not_348_out, not_349_out, not_350_out, not_351_out, not_352_out, not_353_out);
  and and_73 (and_73_out, not_354_out, not_355_out, not_356_out);
  and and_74 (and_74_out, not_357_out, not_358_out, not_359_out, not_360_out, not_361_out, not_362_out, not_363_out);
  and and_75 (and_75_out, not_364_out, not_365_out, not_366_out, not_367_out, not_368_out, not_369_out, not_370_out);
  and and_76 (and_76_out, not_371_out, not_372_out, not_373_out);
  and and_77 (and_77_out, not_374_out, not_375_out, not_376_out, not_377_out, not_378_out, not_379_out, not_380_out);
  and and_78 (and_78_out, not_381_out, not_382_out, not_383_out, not_384_out, not_385_out, not_386_out, not_387_out);
  and and_79 (and_79_out, not_388_out, not_389_out, not_390_out);
  and and_80 (and_80_out, not_391_out, not_392_out, not_393_out, not_394_out, not_395_out, not_396_out, not_397_out);
  and and_81 (and_81_out, not_398_out, not_399_out, not_400_out, not_401_out, not_402_out, not_403_out, not_404_out);
  and and_82 (and_82_out, not_405_out, not_406_out, not_407_out);
  and and_83 (and_83_out, not_408_out, not_409_out, not_410_out, not_411_out, not_412_out, not_413_out, not_414_out);
  and and_84 (and_84_out, not_415_out, not_416_out, not_417_out, not_418_out, not_419_out, not_420_out, not_421_out);
  and and_85 (and_85_out, not_422_out, not_423_out, not_424_out);
  and and_86 (and_86_out, not_425_out, not_426_out, not_427_out, not_428_out, not_429_out, not_430_out, not_431_out);
  and and_87 (and_87_out, not_432_out, not_433_out, not_434_out, not_435_out, not_436_out, not_437_out, not_438_out);
  and and_88 (and_88_out, not_439_out, not_440_out, not_441_out);
  and and_89 (and_89_out, not_442_out, not_443_out, not_444_out, not_445_out, not_446_out, not_447_out, not_448_out);
  and and_90 (and_90_out, not_449_out, not_450_out, not_451_out, not_452_out, not_453_out, not_454_out, not_455_out);
  and and_91 (and_91_out, not_456_out, not_457_out, not_458_out);
  and and_92 (and_92_out, not_459_out, not_460_out, not_461_out, not_462_out, not_463_out, not_464_out, not_465_out);
  and and_93 (and_93_out, not_466_out, not_467_out, not_468_out);
  and and_94 (and_94_out, not_469_out, not_470_out, not_471_out, not_472_out, not_473_out, not_474_out, not_475_out);
  and and_95 (and_95_out, not_476_out, not_477_out, not_478_out);
  and and_96 (and_96_out, not_479_out, not_480_out, not_481_out, not_482_out, not_483_out, not_484_out, not_485_out);
  and and_97 (and_97_out, not_486_out, not_487_out, not_488_out);
  and and_98 (and_98_out, not_489_out, not_490_out, not_491_out, not_492_out, not_493_out, not_494_out, not_495_out);
  and and_99 (and_99_out, and_67_out, and_68_out, and_69_out);
  and and_100 (and_100_out, and_70_out, and_71_out, and_72_out);
  and and_101 (and_101_out, and_73_out, and_74_out, and_75_out);
  and and_102 (and_102_out, and_76_out, and_77_out, and_78_out);
  and and_103 (and_103_out, and_79_out, and_80_out, and_81_out);
  and and_104 (and_104_out, and_82_out, and_83_out, and_84_out);
  and and_105 (and_105_out, and_85_out, and_86_out, and_87_out);
  and and_106 (and_106_out, and_88_out, and_89_out, and_90_out);
  and and_107 (and_107_out, and_91_out, and_92_out);
  and and_108 (and_108_out, and_93_out, and_94_out);
  and and_109 (and_109_out, and_95_out, and_96_out);
  and and_110 (and_110_out, and_97_out, and_98_out);
  or or_7 (ALUctr[1], and_99_out, and_100_out, and_101_out, and_102_out, and_103_out, and_104_out, and_105_out, and_106_out, and_107_out, and_108_out, and_109_out, and_110_out);
  not not_496 (not_496_out, subtractor_86_out[0]);
  Subtractor #(.width(3)) subtractor_86 (
    .a(INSTRUCTION[14:12]), .b(3'b000), .out(subtractor_86_out));  // open: bin, bout
  not not_497 (not_497_out, subtractor_86_out[1]);
  not not_498 (not_498_out, subtractor_86_out[2]);
  not not_499 (not_499_out, subtractor_87_out[0]);
  not not_500 (not_500_out, subtractor_87_out[1]);
  not not_501 (not_501_out, subtractor_87_out[2]);
  Subtractor #(.width(7)) subtractor_87 (
    .a(INSTRUCTION[31:25]), .b(7'b0100000), .out(subtractor_87_out));  // open: bin, bout
  not not_502 (not_502_out, subtractor_87_out[3]);
  not not_503 (not_503_out, subtractor_87_out[4]);
  not not_504 (not_504_out, subtractor_87_out[5]);
  not not_505 (not_505_out, subtractor_87_out[6]);
  not not_506 (not_506_out, subtractor_88_out[0]);
  not not_507 (not_507_out, subtractor_88_out[1]);
  not not_508 (not_508_out, subtractor_88_out[2]);
  Subtractor #(.width(7)) subtractor_88 (
    .a(INSTRUCTION[6:0]), .b(7'b0110011), .out(subtractor_88_out));  // open: bin, bout
  not not_509 (not_509_out, subtractor_88_out[3]);
  not not_510 (not_510_out, subtractor_88_out[4]);
  not not_511 (not_511_out, subtractor_88_out[5]);
  not not_512 (not_512_out, subtractor_88_out[6]);
  not not_513 (not_513_out, subtractor_89_out[0]);
  not not_514 (not_514_out, subtractor_89_out[1]);
  Subtractor #(.width(3)) subtractor_89 (
    .a(INSTRUCTION[14:12]), .b(3'b001), .out(subtractor_89_out));  // open: bin, bout
  not not_515 (not_515_out, subtractor_89_out[2]);
  not not_516 (not_516_out, subtractor_90_out[0]);
  not not_517 (not_517_out, subtractor_90_out[1]);
  not not_518 (not_518_out, subtractor_90_out[2]);
  not not_519 (not_519_out, subtractor_90_out[3]);
  Subtractor #(.width(7)) subtractor_90 (
    .a(INSTRUCTION[31:25]), .b({7{1'b0}}), .out(subtractor_90_out));  // open: bin, bout
  not not_520 (not_520_out, subtractor_90_out[4]);
  not not_521 (not_521_out, subtractor_90_out[5]);
  not not_522 (not_522_out, subtractor_90_out[6]);
  not not_523 (not_523_out, subtractor_91_out[0]);
  not not_524 (not_524_out, subtractor_91_out[1]);
  not not_525 (not_525_out, subtractor_91_out[2]);
  Subtractor #(.width(7)) subtractor_91 (
    .a(INSTRUCTION[6:0]), .b(7'b0110011), .out(subtractor_91_out));  // open: bin, bout
  not not_526 (not_526_out, subtractor_91_out[3]);
  not not_527 (not_527_out, subtractor_91_out[4]);
  not not_528 (not_528_out, subtractor_91_out[5]);
  not not_529 (not_529_out, subtractor_91_out[6]);
  not not_530 (not_530_out, subtractor_92_out[0]);
  Subtractor #(.width(3)) subtractor_92 (
    .a(INSTRUCTION[14:12]), .b(3'b001), .out(subtractor_92_out));  // open: bin, bout
  not not_531 (not_531_out, subtractor_92_out[1]);
  not not_532 (not_532_out, subtractor_92_out[2]);
  not not_533 (not_533_out, subtractor_93_out[0]);
  not not_534 (not_534_out, subtractor_93_out[1]);
  not not_535 (not_535_out, subtractor_93_out[2]);
  not not_536 (not_536_out, subtractor_93_out[3]);
  Subtractor #(.width(7)) subtractor_93 (
    .a(INSTRUCTION[31:25]), .b(7'b0000001), .out(subtractor_93_out));  // open: bin, bout
  not not_537 (not_537_out, subtractor_93_out[4]);
  not not_538 (not_538_out, subtractor_93_out[5]);
  not not_539 (not_539_out, subtractor_93_out[6]);
  not not_540 (not_540_out, subtractor_94_out[0]);
  not not_541 (not_541_out, subtractor_94_out[1]);
  not not_542 (not_542_out, subtractor_94_out[2]);
  Subtractor #(.width(7)) subtractor_94 (
    .a(INSTRUCTION[6:0]), .b(7'b0110011), .out(subtractor_94_out));  // open: bin, bout
  not not_543 (not_543_out, subtractor_94_out[3]);
  not not_544 (not_544_out, subtractor_94_out[4]);
  not not_545 (not_545_out, subtractor_94_out[5]);
  not not_546 (not_546_out, subtractor_94_out[6]);
  not not_547 (not_547_out, subtractor_95_out[0]);
  Subtractor #(.width(3)) subtractor_95 (
    .a(INSTRUCTION[14:12]), .b(3'b010), .out(subtractor_95_out));  // open: bin, bout
  not not_548 (not_548_out, subtractor_95_out[1]);
  not not_549 (not_549_out, subtractor_95_out[2]);
  not not_550 (not_550_out, subtractor_96_out[0]);
  not not_551 (not_551_out, subtractor_96_out[1]);
  not not_552 (not_552_out, subtractor_96_out[2]);
  Subtractor #(.width(7)) subtractor_96 (
    .a(INSTRUCTION[31:25]), .b({7{1'b0}}), .out(subtractor_96_out));  // open: bin, bout
  not not_553 (not_553_out, subtractor_96_out[3]);
  not not_554 (not_554_out, subtractor_96_out[4]);
  not not_555 (not_555_out, subtractor_96_out[5]);
  not not_556 (not_556_out, subtractor_96_out[6]);
  not not_557 (not_557_out, subtractor_97_out[0]);
  not not_558 (not_558_out, subtractor_97_out[1]);
  not not_559 (not_559_out, subtractor_97_out[2]);
  not not_560 (not_560_out, subtractor_97_out[3]);
  Subtractor #(.width(7)) subtractor_97 (
    .a(INSTRUCTION[6:0]), .b(7'b0110011), .out(subtractor_97_out));  // open: bin, bout
  not not_561 (not_561_out, subtractor_97_out[4]);
  not not_562 (not_562_out, subtractor_97_out[5]);
  not not_563 (not_563_out, subtractor_97_out[6]);
  not not_564 (not_564_out, subtractor_98_out[0]);
  not not_565 (not_565_out, subtractor_98_out[1]);
  Subtractor #(.width(3)) subtractor_98 (
    .a(INSTRUCTION[14:12]), .b(3'b101), .out(subtractor_98_out));  // open: bin, bout
  not not_566 (not_566_out, subtractor_98_out[2]);
  not not_567 (not_567_out, subtractor_99_out[0]);
  not not_568 (not_568_out, subtractor_99_out[1]);
  not not_569 (not_569_out, subtractor_99_out[2]);
  not not_570 (not_570_out, subtractor_99_out[3]);
  Subtractor #(.width(7)) subtractor_99 (
    .a(INSTRUCTION[31:25]), .b({7{1'b0}}), .out(subtractor_99_out));  // open: bin, bout
  not not_571 (not_571_out, subtractor_99_out[4]);
  not not_572 (not_572_out, subtractor_99_out[5]);
  not not_573 (not_573_out, subtractor_99_out[6]);
  not not_574 (not_574_out, subtractor_100_out[0]);
  not not_575 (not_575_out, subtractor_100_out[1]);
  not not_576 (not_576_out, subtractor_100_out[2]);
  not not_577 (not_577_out, subtractor_100_out[3]);
  Subtractor #(.width(7)) subtractor_100 (
    .a(INSTRUCTION[6:0]), .b(7'b0110011), .out(subtractor_100_out));  // open: bin, bout
  not not_578 (not_578_out, subtractor_100_out[4]);
  not not_579 (not_579_out, subtractor_100_out[5]);
  not not_580 (not_580_out, subtractor_100_out[6]);
  not not_581 (not_581_out, subtractor_101_out[0]);
  Subtractor #(.width(3)) subtractor_101 (
    .a(INSTRUCTION[14:12]), .b(3'b001), .out(subtractor_101_out));  // open: bin, bout
  not not_582 (not_582_out, subtractor_101_out[1]);
  not not_583 (not_583_out, subtractor_101_out[2]);
  not not_584 (not_584_out, subtractor_102_out[0]);
  not not_585 (not_585_out, subtractor_102_out[1]);
  not not_586 (not_586_out, subtractor_102_out[2]);
  Subtractor #(.width(7)) subtractor_102 (
    .a(INSTRUCTION[31:25]), .b({7{1'b0}}), .out(subtractor_102_out));  // open: bin, bout
  not not_587 (not_587_out, subtractor_102_out[3]);
  not not_588 (not_588_out, subtractor_102_out[4]);
  not not_589 (not_589_out, subtractor_102_out[5]);
  not not_590 (not_590_out, subtractor_102_out[6]);
  not not_591 (not_591_out, subtractor_103_out[0]);
  not not_592 (not_592_out, subtractor_103_out[1]);
  not not_593 (not_593_out, subtractor_103_out[2]);
  not not_594 (not_594_out, subtractor_103_out[3]);
  Subtractor #(.width(7)) subtractor_103 (
    .a(INSTRUCTION[6:0]), .b(7'b0010011), .out(subtractor_103_out));  // open: bin, bout
  not not_595 (not_595_out, subtractor_103_out[4]);
  not not_596 (not_596_out, subtractor_103_out[5]);
  not not_597 (not_597_out, subtractor_103_out[6]);
  not not_598 (not_598_out, subtractor_104_out[0]);
  Subtractor #(.width(3)) subtractor_104 (
    .a(INSTRUCTION[14:12]), .b(3'b010), .out(subtractor_104_out));  // open: bin, bout
  not not_599 (not_599_out, subtractor_104_out[1]);
  not not_600 (not_600_out, subtractor_104_out[2]);
  not not_601 (not_601_out, subtractor_105_out[0]);
  not not_602 (not_602_out, subtractor_105_out[1]);
  not not_603 (not_603_out, subtractor_105_out[2]);
  not not_604 (not_604_out, subtractor_105_out[3]);
  Subtractor #(.width(7)) subtractor_105 (
    .a(INSTRUCTION[6:0]), .b(7'b0010011), .out(subtractor_105_out));  // open: bin, bout
  not not_605 (not_605_out, subtractor_105_out[4]);
  not not_606 (not_606_out, subtractor_105_out[5]);
  not not_607 (not_607_out, subtractor_105_out[6]);
  not not_608 (not_608_out, subtractor_106_out[0]);
  Subtractor #(.width(3)) subtractor_106 (
    .a(INSTRUCTION[14:12]), .b(3'b101), .out(subtractor_106_out));  // open: bin, bout
  not not_609 (not_609_out, subtractor_106_out[1]);
  not not_610 (not_610_out, subtractor_106_out[2]);
  not not_611 (not_611_out, subtractor_107_out[0]);
  not not_612 (not_612_out, subtractor_107_out[1]);
  not not_613 (not_613_out, subtractor_107_out[2]);
  Subtractor #(.width(7)) subtractor_107 (
    .a(INSTRUCTION[31:25]), .b({7{1'b0}}), .out(subtractor_107_out));  // open: bin, bout
  not not_614 (not_614_out, subtractor_107_out[3]);
  not not_615 (not_615_out, subtractor_107_out[4]);
  not not_616 (not_616_out, subtractor_107_out[5]);
  not not_617 (not_617_out, subtractor_107_out[6]);
  not not_618 (not_618_out, subtractor_108_out[0]);
  not not_619 (not_619_out, subtractor_108_out[1]);
  not not_620 (not_620_out, subtractor_108_out[2]);
  Subtractor #(.width(7)) subtractor_108 (
    .a(INSTRUCTION[6:0]), .b(7'b0010011), .out(subtractor_108_out));  // open: bin, bout
  not not_621 (not_621_out, subtractor_108_out[3]);
  not not_622 (not_622_out, subtractor_108_out[4]);
  not not_623 (not_623_out, subtractor_108_out[5]);
  not not_624 (not_624_out, subtractor_108_out[6]);
  not not_625 (not_625_out, subtractor_109_out[0]);
  Subtractor #(.width(3)) subtractor_109 (
    .a(INSTRUCTION[14:12]), .b(3'b101), .out(subtractor_109_out));  // open: bin, bout
  not not_626 (not_626_out, subtractor_109_out[1]);
  not not_627 (not_627_out, subtractor_109_out[2]);
  not not_628 (not_628_out, subtractor_110_out[0]);
  not not_629 (not_629_out, subtractor_110_out[1]);
  not not_630 (not_630_out, subtractor_110_out[2]);
  not not_631 (not_631_out, subtractor_110_out[3]);
  Subtractor #(.width(7)) subtractor_110 (
    .a(INSTRUCTION[31:25]), .b(7'b0100000), .out(subtractor_110_out));  // open: bin, bout
  not not_632 (not_632_out, subtractor_110_out[4]);
  not not_633 (not_633_out, subtractor_110_out[5]);
  not not_634 (not_634_out, subtractor_110_out[6]);
  not not_635 (not_635_out, subtractor_111_out[0]);
  not not_636 (not_636_out, subtractor_111_out[1]);
  not not_637 (not_637_out, subtractor_111_out[2]);
  not not_638 (not_638_out, subtractor_111_out[3]);
  Subtractor #(.width(7)) subtractor_111 (
    .a(INSTRUCTION[6:0]), .b(7'b0010011), .out(subtractor_111_out));  // open: bin, bout
  not not_639 (not_639_out, subtractor_111_out[4]);
  not not_640 (not_640_out, subtractor_111_out[5]);
  not not_641 (not_641_out, subtractor_111_out[6]);
  not not_642 (not_642_out, subtractor_112_out[0]);
  not not_643 (not_643_out, subtractor_112_out[1]);
  Subtractor #(.width(3)) subtractor_112 (
    .a(INSTRUCTION[14:12]), .b(3'b000), .out(subtractor_112_out));  // open: bin, bout
  not not_644 (not_644_out, subtractor_112_out[2]);
  not not_645 (not_645_out, subtractor_113_out[0]);
  not not_646 (not_646_out, subtractor_113_out[1]);
  not not_647 (not_647_out, subtractor_113_out[2]);
  not not_648 (not_648_out, subtractor_113_out[3]);
  Subtractor #(.width(7)) subtractor_113 (
    .a(INSTRUCTION[6:0]), .b(7'b1100011), .out(subtractor_113_out));  // open: bin, bout
  not not_649 (not_649_out, subtractor_113_out[4]);
  not not_650 (not_650_out, subtractor_113_out[5]);
  not not_651 (not_651_out, subtractor_113_out[6]);
  not not_652 (not_652_out, subtractor_114_out[0]);
  not not_653 (not_653_out, subtractor_114_out[1]);
  Subtractor #(.width(3)) subtractor_114 (
    .a(INSTRUCTION[14:12]), .b(3'b100), .out(subtractor_114_out));  // open: bin, bout
  not not_654 (not_654_out, subtractor_114_out[2]);
  not not_655 (not_655_out, subtractor_115_out[0]);
  not not_656 (not_656_out, subtractor_115_out[1]);
  not not_657 (not_657_out, subtractor_115_out[2]);
  Subtractor #(.width(7)) subtractor_115 (
    .a(INSTRUCTION[6:0]), .b(7'b1100011), .out(subtractor_115_out));  // open: bin, bout
  not not_658 (not_658_out, subtractor_115_out[3]);
  not not_659 (not_659_out, subtractor_115_out[4]);
  not not_660 (not_660_out, subtractor_115_out[5]);
  not not_661 (not_661_out, subtractor_115_out[6]);
  not not_662 (not_662_out, subtractor_116_out[0]);
  not not_663 (not_663_out, subtractor_116_out[1]);
  Subtractor #(.width(3)) subtractor_116 (
    .a(INSTRUCTION[14:12]), .b(3'b001), .out(subtractor_116_out));  // open: bin, bout
  not not_664 (not_664_out, subtractor_116_out[2]);
  not not_665 (not_665_out, subtractor_117_out[0]);
  not not_666 (not_666_out, subtractor_117_out[1]);
  not not_667 (not_667_out, subtractor_117_out[2]);
  Subtractor #(.width(7)) subtractor_117 (
    .a(INSTRUCTION[6:0]), .b(7'b1100011), .out(subtractor_117_out));  // open: bin, bout
  not not_668 (not_668_out, subtractor_117_out[3]);
  not not_669 (not_669_out, subtractor_117_out[4]);
  not not_670 (not_670_out, subtractor_117_out[5]);
  not not_671 (not_671_out, subtractor_117_out[6]);
  not not_672 (not_672_out, subtractor_118_out[0]);
  not not_673 (not_673_out, subtractor_118_out[1]);
  not not_674 (not_674_out, subtractor_118_out[2]);
  not not_675 (not_675_out, subtractor_118_out[3]);
  Subtractor #(.width(7)) subtractor_118 (
    .a(INSTRUCTION[6:0]), .b(7'b0110111), .out(subtractor_118_out));  // open: bin, bout
  not not_676 (not_676_out, subtractor_118_out[4]);
  not not_677 (not_677_out, subtractor_118_out[5]);
  not not_678 (not_678_out, subtractor_118_out[6]);
  and and_111 (and_111_out, not_496_out, not_497_out, not_498_out);
  and and_112 (and_112_out, not_499_out, not_500_out, not_501_out, not_502_out, not_503_out, not_504_out, not_505_out);
  and and_113 (and_113_out, not_506_out, not_507_out, not_508_out, not_509_out, not_510_out, not_511_out, not_512_out);
  and and_114 (and_114_out, not_513_out, not_514_out, not_515_out);
  and and_115 (and_115_out, not_516_out, not_517_out, not_518_out, not_519_out, not_520_out, not_521_out, not_522_out);
  and and_116 (and_116_out, not_523_out, not_524_out, not_525_out, not_526_out, not_527_out, not_528_out, not_529_out);
  and and_117 (and_117_out, not_530_out, not_531_out, not_532_out);
  and and_118 (and_118_out, not_533_out, not_534_out, not_535_out, not_536_out, not_537_out, not_538_out, not_539_out);
  and and_119 (and_119_out, not_540_out, not_541_out, not_542_out, not_543_out, not_544_out, not_545_out, not_546_out);
  and and_120 (and_120_out, not_547_out, not_548_out, not_549_out);
  and and_121 (and_121_out, not_550_out, not_551_out, not_552_out, not_553_out, not_554_out, not_555_out, not_556_out);
  and and_122 (and_122_out, not_557_out, not_558_out, not_559_out, not_560_out, not_561_out, not_562_out, not_563_out);
  and and_123 (and_123_out, not_564_out, not_565_out, not_566_out);
  and and_124 (and_124_out, not_567_out, not_568_out, not_569_out, not_570_out, not_571_out, not_572_out, not_573_out);
  and and_125 (and_125_out, not_574_out, not_575_out, not_576_out, not_577_out, not_578_out, not_579_out, not_580_out);
  and and_126 (and_126_out, not_581_out, not_582_out, not_583_out);
  and and_127 (and_127_out, not_584_out, not_585_out, not_586_out, not_587_out, not_588_out, not_589_out, not_590_out);
  and and_128 (and_128_out, not_591_out, not_592_out, not_593_out, not_594_out, not_595_out, not_596_out, not_597_out);
  and and_129 (and_129_out, not_598_out, not_599_out, not_600_out);
  and and_130 (and_130_out, not_601_out, not_602_out, not_603_out, not_604_out, not_605_out, not_606_out, not_607_out);
  and and_131 (and_131_out, not_608_out, not_609_out, not_610_out);
  and and_132 (and_132_out, not_611_out, not_612_out, not_613_out, not_614_out, not_615_out, not_616_out, not_617_out);
  and and_133 (and_133_out, not_618_out, not_619_out, not_620_out, not_621_out, not_622_out, not_623_out, not_624_out);
  and and_134 (and_134_out, not_625_out, not_626_out, not_627_out);
  and and_135 (and_135_out, not_628_out, not_629_out, not_630_out, not_631_out, not_632_out, not_633_out, not_634_out);
  and and_136 (and_136_out, not_635_out, not_636_out, not_637_out, not_638_out, not_639_out, not_640_out, not_641_out);
  and and_137 (and_137_out, not_642_out, not_643_out, not_644_out);
  and and_138 (and_138_out, not_645_out, not_646_out, not_647_out, not_648_out, not_649_out, not_650_out, not_651_out);
  and and_139 (and_139_out, not_652_out, not_653_out, not_654_out);
  and and_140 (and_140_out, not_655_out, not_656_out, not_657_out, not_658_out, not_659_out, not_660_out, not_661_out);
  and and_141 (and_141_out, not_662_out, not_663_out, not_664_out);
  and and_142 (and_142_out, not_665_out, not_666_out, not_667_out, not_668_out, not_669_out, not_670_out, not_671_out);
  and and_143 (and_143_out, not_672_out, not_673_out, not_674_out, not_675_out, not_676_out, not_677_out, not_678_out);
  and and_144 (and_144_out, and_111_out, and_112_out, and_113_out);
  and and_145 (and_145_out, and_114_out, and_115_out, and_116_out);
  and and_146 (and_146_out, and_117_out, and_118_out, and_119_out);
  and and_147 (and_147_out, and_120_out, and_121_out, and_122_out);
  and and_148 (and_148_out, and_123_out, and_124_out, and_125_out);
  and and_149 (and_149_out, and_126_out, and_127_out, and_128_out);
  and and_150 (and_150_out, and_129_out, and_130_out);
  and and_151 (and_151_out, and_131_out, and_132_out, and_133_out);
  and and_152 (and_152_out, and_134_out, and_135_out, and_136_out);
  and and_153 (and_153_out, and_137_out, and_138_out);
  and and_154 (and_154_out, and_139_out, and_140_out);
  and and_155 (and_155_out, and_141_out, and_142_out);
  or or_8 (ALUctr[2], and_144_out, and_145_out, and_146_out, and_147_out, and_148_out, and_149_out, and_150_out, and_151_out, and_152_out, and_153_out, and_154_out, and_155_out, and_143_out);
  not not_679 (not_679_out, subtractor_119_out[0]);
  not not_680 (not_680_out, subtractor_119_out[1]);
  Subtractor #(.width(3)) subtractor_119 (
    .a(INSTRUCTION[14:12]), .b(3'b000), .out(subtractor_119_out));  // open: bin, bout
  not not_681 (not_681_out, subtractor_119_out[2]);
  not not_682 (not_682_out, subtractor_120_out[0]);
  not not_683 (not_683_out, subtractor_120_out[1]);
  not not_684 (not_684_out, subtractor_120_out[2]);
  Subtractor #(.width(7)) subtractor_120 (
    .a(INSTRUCTION[31:25]), .b(7'b0000001), .out(subtractor_120_out));  // open: bin, bout
  not not_685 (not_685_out, subtractor_120_out[3]);
  not not_686 (not_686_out, subtractor_120_out[4]);
  not not_687 (not_687_out, subtractor_120_out[5]);
  not not_688 (not_688_out, subtractor_120_out[6]);
  not not_689 (not_689_out, subtractor_121_out[0]);
  not not_690 (not_690_out, subtractor_121_out[1]);
  not not_691 (not_691_out, subtractor_121_out[2]);
  Subtractor #(.width(7)) subtractor_121 (
    .a(INSTRUCTION[6:0]), .b(7'b0110011), .out(subtractor_121_out));  // open: bin, bout
  not not_692 (not_692_out, subtractor_121_out[3]);
  not not_693 (not_693_out, subtractor_121_out[4]);
  not not_694 (not_694_out, subtractor_121_out[5]);
  not not_695 (not_695_out, subtractor_121_out[6]);
  not not_696 (not_696_out, subtractor_122_out[0]);
  Subtractor #(.width(3)) subtractor_122 (
    .a(INSTRUCTION[14:12]), .b(3'b000), .out(subtractor_122_out));  // open: bin, bout
  not not_697 (not_697_out, subtractor_122_out[1]);
  not not_698 (not_698_out, subtractor_122_out[2]);
  not not_699 (not_699_out, subtractor_123_out[0]);
  not not_700 (not_700_out, subtractor_123_out[1]);
  not not_701 (not_701_out, subtractor_123_out[2]);
  not not_702 (not_702_out, subtractor_123_out[3]);
  Subtractor #(.width(7)) subtractor_123 (
    .a(INSTRUCTION[31:25]), .b(7'b0100000), .out(subtractor_123_out));  // open: bin, bout
  not not_703 (not_703_out, subtractor_123_out[4]);
  not not_704 (not_704_out, subtractor_123_out[5]);
  not not_705 (not_705_out, subtractor_123_out[6]);
  not not_706 (not_706_out, subtractor_124_out[0]);
  not not_707 (not_707_out, subtractor_124_out[1]);
  not not_708 (not_708_out, subtractor_124_out[2]);
  Subtractor #(.width(7)) subtractor_124 (
    .a(INSTRUCTION[6:0]), .b(7'b0110011), .out(subtractor_124_out));  // open: bin, bout
  not not_709 (not_709_out, subtractor_124_out[3]);
  not not_710 (not_710_out, subtractor_124_out[4]);
  not not_711 (not_711_out, subtractor_124_out[5]);
  not not_712 (not_712_out, subtractor_124_out[6]);
  not not_713 (not_713_out, subtractor_125_out[0]);
  Subtractor #(.width(3)) subtractor_125 (
    .a(INSTRUCTION[14:12]), .b(3'b001), .out(subtractor_125_out));  // open: bin, bout
  not not_714 (not_714_out, subtractor_125_out[1]);
  not not_715 (not_715_out, subtractor_125_out[2]);
  not not_716 (not_716_out, subtractor_126_out[0]);
  not not_717 (not_717_out, subtractor_126_out[1]);
  not not_718 (not_718_out, subtractor_126_out[2]);
  not not_719 (not_719_out, subtractor_126_out[3]);
  Subtractor #(.width(7)) subtractor_126 (
    .a(INSTRUCTION[31:25]), .b(7'b0000001), .out(subtractor_126_out));  // open: bin, bout
  not not_720 (not_720_out, subtractor_126_out[4]);
  not not_721 (not_721_out, subtractor_126_out[5]);
  not not_722 (not_722_out, subtractor_126_out[6]);
  not not_723 (not_723_out, subtractor_127_out[0]);
  not not_724 (not_724_out, subtractor_127_out[1]);
  not not_725 (not_725_out, subtractor_127_out[2]);
  not not_726 (not_726_out, subtractor_127_out[3]);
  Subtractor #(.width(7)) subtractor_127 (
    .a(INSTRUCTION[6:0]), .b(7'b0110011), .out(subtractor_127_out));  // open: bin, bout
  not not_727 (not_727_out, subtractor_127_out[4]);
  not not_728 (not_728_out, subtractor_127_out[5]);
  not not_729 (not_729_out, subtractor_127_out[6]);
  not not_730 (not_730_out, subtractor_128_out[0]);
  Subtractor #(.width(3)) subtractor_128 (
    .a(INSTRUCTION[14:12]), .b(3'b011), .out(subtractor_128_out));  // open: bin, bout
  not not_731 (not_731_out, subtractor_128_out[1]);
  not not_732 (not_732_out, subtractor_128_out[2]);
  not not_733 (not_733_out, subtractor_129_out[0]);
  not not_734 (not_734_out, subtractor_129_out[1]);
  not not_735 (not_735_out, subtractor_129_out[2]);
  not not_736 (not_736_out, subtractor_129_out[3]);
  Subtractor #(.width(7)) subtractor_129 (
    .a(INSTRUCTION[31:25]), .b(7'b0000001), .out(subtractor_129_out));  // open: bin, bout
  not not_737 (not_737_out, subtractor_129_out[4]);
  not not_738 (not_738_out, subtractor_129_out[5]);
  not not_739 (not_739_out, subtractor_129_out[6]);
  not not_740 (not_740_out, subtractor_130_out[0]);
  not not_741 (not_741_out, subtractor_130_out[1]);
  not not_742 (not_742_out, subtractor_130_out[2]);
  Subtractor #(.width(7)) subtractor_130 (
    .a(INSTRUCTION[6:0]), .b(7'b0110011), .out(subtractor_130_out));  // open: bin, bout
  not not_743 (not_743_out, subtractor_130_out[3]);
  not not_744 (not_744_out, subtractor_130_out[4]);
  not not_745 (not_745_out, subtractor_130_out[5]);
  not not_746 (not_746_out, subtractor_130_out[6]);
  not not_747 (not_747_out, subtractor_131_out[0]);
  not not_748 (not_748_out, subtractor_131_out[1]);
  Subtractor #(.width(3)) subtractor_131 (
    .a(INSTRUCTION[14:12]), .b(3'b101), .out(subtractor_131_out));  // open: bin, bout
  not not_749 (not_749_out, subtractor_131_out[2]);
  not not_750 (not_750_out, subtractor_132_out[0]);
  not not_751 (not_751_out, subtractor_132_out[1]);
  not not_752 (not_752_out, subtractor_132_out[2]);
  not not_753 (not_753_out, subtractor_132_out[3]);
  Subtractor #(.width(7)) subtractor_132 (
    .a(INSTRUCTION[31:25]), .b(7'b0000001), .out(subtractor_132_out));  // open: bin, bout
  not not_754 (not_754_out, subtractor_132_out[4]);
  not not_755 (not_755_out, subtractor_132_out[5]);
  not not_756 (not_756_out, subtractor_132_out[6]);
  not not_757 (not_757_out, subtractor_133_out[0]);
  not not_758 (not_758_out, subtractor_133_out[1]);
  not not_759 (not_759_out, subtractor_133_out[2]);
  Subtractor #(.width(7)) subtractor_133 (
    .a(INSTRUCTION[6:0]), .b(7'b0110011), .out(subtractor_133_out));  // open: bin, bout
  not not_760 (not_760_out, subtractor_133_out[3]);
  not not_761 (not_761_out, subtractor_133_out[4]);
  not not_762 (not_762_out, subtractor_133_out[5]);
  not not_763 (not_763_out, subtractor_133_out[6]);
  not not_764 (not_764_out, subtractor_134_out[0]);
  not not_765 (not_765_out, subtractor_134_out[1]);
  Subtractor #(.width(3)) subtractor_134 (
    .a(INSTRUCTION[14:12]), .b(3'b111), .out(subtractor_134_out));  // open: bin, bout
  not not_766 (not_766_out, subtractor_134_out[2]);
  not not_767 (not_767_out, subtractor_135_out[0]);
  not not_768 (not_768_out, subtractor_135_out[1]);
  not not_769 (not_769_out, subtractor_135_out[2]);
  not not_770 (not_770_out, subtractor_135_out[3]);
  Subtractor #(.width(7)) subtractor_135 (
    .a(INSTRUCTION[31:25]), .b(7'b0000001), .out(subtractor_135_out));  // open: bin, bout
  not not_771 (not_771_out, subtractor_135_out[4]);
  not not_772 (not_772_out, subtractor_135_out[5]);
  not not_773 (not_773_out, subtractor_135_out[6]);
  not not_774 (not_774_out, subtractor_136_out[0]);
  not not_775 (not_775_out, subtractor_136_out[1]);
  not not_776 (not_776_out, subtractor_136_out[2]);
  not not_777 (not_777_out, subtractor_136_out[3]);
  Subtractor #(.width(7)) subtractor_136 (
    .a(INSTRUCTION[6:0]), .b(7'b0110011), .out(subtractor_136_out));  // open: bin, bout
  not not_778 (not_778_out, subtractor_136_out[4]);
  not not_779 (not_779_out, subtractor_136_out[5]);
  not not_780 (not_780_out, subtractor_136_out[6]);
  not not_781 (not_781_out, subtractor_137_out[0]);
  Subtractor #(.width(3)) subtractor_137 (
    .a(INSTRUCTION[14:12]), .b(3'b000), .out(subtractor_137_out));  // open: bin, bout
  not not_782 (not_782_out, subtractor_137_out[1]);
  not not_783 (not_783_out, subtractor_137_out[2]);
  not not_784 (not_784_out, subtractor_138_out[0]);
  not not_785 (not_785_out, subtractor_138_out[1]);
  not not_786 (not_786_out, subtractor_138_out[2]);
  not not_787 (not_787_out, subtractor_138_out[3]);
  Subtractor #(.width(7)) subtractor_138 (
    .a(INSTRUCTION[6:0]), .b(7'b1100011), .out(subtractor_138_out));  // open: bin, bout
  not not_788 (not_788_out, subtractor_138_out[4]);
  not not_789 (not_789_out, subtractor_138_out[5]);
  not not_790 (not_790_out, subtractor_138_out[6]);
  not not_791 (not_791_out, subtractor_139_out[0]);
  not not_792 (not_792_out, subtractor_139_out[1]);
  Subtractor #(.width(3)) subtractor_139 (
    .a(INSTRUCTION[14:12]), .b(3'b001), .out(subtractor_139_out));  // open: bin, bout
  not not_793 (not_793_out, subtractor_139_out[2]);
  not not_794 (not_794_out, subtractor_140_out[0]);
  not not_795 (not_795_out, subtractor_140_out[1]);
  not not_796 (not_796_out, subtractor_140_out[2]);
  not not_797 (not_797_out, subtractor_140_out[3]);
  Subtractor #(.width(7)) subtractor_140 (
    .a(INSTRUCTION[6:0]), .b(7'b1100011), .out(subtractor_140_out));  // open: bin, bout
  not not_798 (not_798_out, subtractor_140_out[4]);
  not not_799 (not_799_out, subtractor_140_out[5]);
  not not_800 (not_800_out, subtractor_140_out[6]);
  not not_801 (not_801_out, subtractor_141_out[0]);
  not not_802 (not_802_out, subtractor_141_out[1]);
  not not_803 (not_803_out, subtractor_141_out[2]);
  not not_804 (not_804_out, subtractor_141_out[3]);
  Subtractor #(.width(7)) subtractor_141 (
    .a(INSTRUCTION[6:0]), .b(7'b0110111), .out(subtractor_141_out));  // open: bin, bout
  not not_805 (not_805_out, subtractor_141_out[4]);
  not not_806 (not_806_out, subtractor_141_out[5]);
  not not_807 (not_807_out, subtractor_141_out[6]);
  Subtractor #(.width(3)) subtractor_142 (
    .a(INSTRUCTION[14:12]), .b(3'b110), .out(subtractor_142_out));  // open: bin, bout
  not not_808 (not_808_out, subtractor_143_out[0]);
  not not_809 (not_809_out, subtractor_143_out[1]);
  not not_810 (not_810_out, subtractor_143_out[2]);
  not not_811 (not_811_out, subtractor_143_out[3]);
  Subtractor #(.width(7)) subtractor_143 (
    .a(INSTRUCTION[6:0]), .b(7'b1100011), .out(subtractor_143_out));  // open: bin, bout
  not not_812 (not_812_out, subtractor_143_out[4]);
  not not_813 (not_813_out, subtractor_143_out[5]);
  not not_814 (not_814_out, subtractor_143_out[6]);
  and and_156 (and_156_out, not_679_out, not_680_out, not_681_out);
  and and_157 (and_157_out, not_682_out, not_683_out, not_684_out, not_685_out, not_686_out, not_687_out, not_688_out);
  and and_158 (and_158_out, not_689_out, not_690_out, not_691_out, not_692_out, not_693_out, not_694_out, not_695_out);
  and and_159 (and_159_out, not_696_out, not_697_out, not_698_out);
  and and_160 (and_160_out, not_699_out, not_700_out, not_701_out, not_702_out, not_703_out, not_704_out, not_705_out);
  and and_161 (and_161_out, not_706_out, not_707_out, not_708_out, not_709_out, not_710_out, not_711_out, not_712_out);
  and and_162 (and_162_out, not_713_out, not_714_out, not_715_out);
  and and_163 (and_163_out, not_716_out, not_717_out, not_718_out, not_719_out, not_720_out, not_721_out, not_722_out);
  and and_164 (and_164_out, not_723_out, not_724_out, not_725_out, not_726_out, not_727_out, not_728_out, not_729_out);
  and and_165 (and_165_out, not_730_out, not_731_out, not_732_out);
  and and_166 (and_166_out, not_733_out, not_734_out, not_735_out, not_736_out, not_737_out, not_738_out, not_739_out);
  and and_167 (and_167_out, not_740_out, not_741_out, not_742_out, not_743_out, not_744_out, not_745_out, not_746_out);
  and and_168 (and_168_out, not_747_out, not_748_out, not_749_out);
  and and_169 (and_169_out, not_750_out, not_751_out, not_752_out, not_753_out, not_754_out, not_755_out, not_756_out);
  and and_170 (and_170_out, not_757_out, not_758_out, not_759_out, not_760_out, not_761_out, not_762_out, not_763_out);
  and and_171 (and_171_out, not_764_out, not_765_out, not_766_out);
  and and_172 (and_172_out, not_767_out, not_768_out, not_769_out, not_770_out, not_771_out, not_772_out, not_773_out);
  and and_173 (and_173_out, not_774_out, not_775_out, not_776_out, not_777_out, not_778_out, not_779_out, not_780_out);
  and and_174 (and_174_out, not_781_out, not_782_out, not_783_out);
  and and_175 (and_175_out, not_784_out, not_785_out, not_786_out, not_787_out, not_788_out, not_789_out, not_790_out);
  and and_176 (and_176_out, not_791_out, not_792_out, not_793_out);
  and and_177 (and_177_out, not_794_out, not_795_out, not_796_out, not_797_out, not_798_out, not_799_out, not_800_out);
  and and_178 (and_178_out, not_801_out, not_802_out, not_803_out, not_804_out, not_805_out, not_806_out, not_807_out);
  not not_815 (not_815_out, subtractor_142_out[0]);
  and and_179 (and_179_out, not_815_out, not_816_out, not_817_out);
  not not_816 (not_816_out, subtractor_142_out[1]);
  not not_817 (not_817_out, subtractor_142_out[2]);
  and and_180 (and_180_out, not_808_out, not_809_out, not_810_out, not_811_out, not_812_out, not_813_out, not_814_out);
  and and_181 (and_181_out, and_156_out, and_157_out, and_158_out);
  and and_182 (and_182_out, and_159_out, and_160_out, and_161_out);
  and and_183 (and_183_out, and_162_out, and_163_out, and_164_out);
  and and_184 (and_184_out, and_165_out, and_166_out, and_167_out);
  and and_185 (and_185_out, and_168_out, and_169_out, and_170_out);
  and and_186 (and_186_out, and_171_out, and_172_out, and_173_out);
  and and_187 (and_187_out, and_174_out, and_175_out);
  and and_188 (and_188_out, and_176_out, and_177_out);
  and and_189 (and_189_out, and_179_out, and_180_out);
  or or_9 (ALUctr[3], and_181_out, and_182_out, and_183_out, and_184_out, and_185_out, and_186_out, and_187_out, and_188_out, and_178_out, and_189_out);

  // Other names for the same wires on the sheet: A1 = ALUctr[0]; A2 = ALUctr[1]; A3 = ALUctr[2]; A4 = ALUctr[3];
  //   E1 = ExtOp[0]; E2 = ExtOp[1]; E3 = ExtOp[2]; opcode[6:0] = INSTRUCTION[6:0]; funct3[2:0] = INSTRUCTION[14:12];
  //   funct7[6:0] = INSTRUCTION[31:25]; L1 = LoadOp[0]; L2 = LoadOp[1]
endmodule
